// Digital circuit 16_bit_dig_disply_tester.dig as structural Verilog
module _16_bit_dig_disply_tester (
  input  clk
);

  wire button_1_out;
  wire [3:0] _16_bit_to_6_7_sec_connector_1_o_2;
  wire [6:0] _16_bit_to_6_7_sec_connector_1_o_3;
  wire [15:0] _16_bit_adder_1_s, _16_bit_multiplexer_1_o, register_1_q;
  wire [34:0] _16_bit_to_6_7_sec_connector_1_o;

  _16_bit_adder _16_bit_adder_1 (.A(register_1_q), .B(16'hb), .S(_16_bit_adder_1_s));  // open: C
  Button button_1 (.out(button_1_out));
  _16_bit_multiplexer _16_bit_multiplexer_1 (
    .A1(_16_bit_adder_1_s), .A2(16'hd499), .S(button_1_out), .O(_16_bit_multiplexer_1_o));
  Register #(.Bits(16)) register_1 (.D(_16_bit_multiplexer_1_o), .C(clk), .en(1'b1), .Q(register_1_q));
  _16_bit_to_6_7_sec_connector _16_bit_to_6_7_sec_connector_1 (
    .I(register_1_q),
    .O({_16_bit_to_6_7_sec_connector_1_o_3, _16_bit_to_6_7_sec_connector_1_o[34:32], _16_bit_to_6_7_sec_connector_1_o_2, _16_bit_to_6_7_sec_connector_1_o[27:0]}));
  Seven_Seg seven_seg_1 (
    .a(_16_bit_to_6_7_sec_connector_1_o[3]), .b(_16_bit_to_6_7_sec_connector_1_o[2]),
    .c(_16_bit_to_6_7_sec_connector_1_o[1]), .d(_16_bit_to_6_7_sec_connector_1_o[0]),
    .e(_16_bit_to_6_7_sec_connector_1_o[4]), .f(_16_bit_to_6_7_sec_connector_1_o[5]),
    .g(_16_bit_to_6_7_sec_connector_1_o[6]), .dp(1'b0));
  Seven_Seg seven_seg_2 (
    .a(_16_bit_to_6_7_sec_connector_1_o[10]), .b(_16_bit_to_6_7_sec_connector_1_o[9]),
    .c(_16_bit_to_6_7_sec_connector_1_o[8]), .d(_16_bit_to_6_7_sec_connector_1_o[7]),
    .e(_16_bit_to_6_7_sec_connector_1_o[11]), .f(_16_bit_to_6_7_sec_connector_1_o[12]),
    .g(_16_bit_to_6_7_sec_connector_1_o[13]), .dp(1'b0));
  Seven_Seg seven_seg_3 (
    .a(_16_bit_to_6_7_sec_connector_1_o[17]), .b(_16_bit_to_6_7_sec_connector_1_o[16]),
    .c(_16_bit_to_6_7_sec_connector_1_o[15]), .d(_16_bit_to_6_7_sec_connector_1_o[14]),
    .e(_16_bit_to_6_7_sec_connector_1_o[18]), .f(_16_bit_to_6_7_sec_connector_1_o[19]),
    .g(_16_bit_to_6_7_sec_connector_1_o[20]), .dp(1'b0));
  Seven_Seg seven_seg_4 (
    .a(_16_bit_to_6_7_sec_connector_1_o[24]), .b(_16_bit_to_6_7_sec_connector_1_o[23]),
    .c(_16_bit_to_6_7_sec_connector_1_o[22]), .d(_16_bit_to_6_7_sec_connector_1_o[21]),
    .e(_16_bit_to_6_7_sec_connector_1_o[25]), .f(_16_bit_to_6_7_sec_connector_1_o[26]),
    .g(_16_bit_to_6_7_sec_connector_1_o[27]), .dp(1'b0));
  Seven_Seg seven_seg_5 (
    .a(_16_bit_to_6_7_sec_connector_1_o_2[3]), .b(_16_bit_to_6_7_sec_connector_1_o_2[2]),
    .c(_16_bit_to_6_7_sec_connector_1_o_2[1]), .d(_16_bit_to_6_7_sec_connector_1_o_2[0]),
    .e(_16_bit_to_6_7_sec_connector_1_o[32]), .f(_16_bit_to_6_7_sec_connector_1_o[33]),
    .g(_16_bit_to_6_7_sec_connector_1_o[34]), .dp(1'b0));
  Seven_Seg seven_seg_6 (
    .a(_16_bit_to_6_7_sec_connector_1_o_3[3]), .b(_16_bit_to_6_7_sec_connector_1_o_3[2]),
    .c(_16_bit_to_6_7_sec_connector_1_o_3[1]), .d(_16_bit_to_6_7_sec_connector_1_o_3[0]),
    .e(_16_bit_to_6_7_sec_connector_1_o_3[4]), .f(_16_bit_to_6_7_sec_connector_1_o_3[5]),
    .g(_16_bit_to_6_7_sec_connector_1_o_3[6]), .dp(1'b0));

  // Notes on the sheet:
  //   clk: Hz: 50
endmodule
