// Digital circuit 16_bit_div_by_10.dig as structural Verilog
module _16_bit_div_by_10 (
  input  [15:0] I,
  output [3:0] O
);

  wire _16_bit_higher_than_9_1_o, _16_bit_higher_than_9_2_o, _16_bit_higher_than_9_3_o,
       _16_bit_higher_than_9_4_o, _16_bit_higher_than_9_5_o, _16_bit_higher_than_9_6_o,
       _16_bit_higher_than_9_7_o, _16_bit_higher_than_9_8_o, _16_bit_higher_than_9_9_o, and_1_out, and_2_out,
       and_3_out, and_4_out, and_5_out, and_6_out, and_7_out, and_8_out;
  wire [3:0] _1_to_4_1_o, _1_to_4_2_o, _1_to_4_3_o, _1_to_4_4_o, _1_to_4_5_o, _1_to_4_6_o, _1_to_4_7_o,
       _1_to_4_8_o, _1_to_4_9_o, and_9_out, and_10_out, and_11_out, and_12_out, and_13_out, and_14_out,
       and_15_out, and_16_out, and_17_out, or_1_out, or_2_out, or_3_out, or_4_out, or_5_out, or_6_out,
       or_7_out;
  wire [15:0] _16_bit_adder_1_s, _16_bit_adder_2_s, _16_bit_adder_3_s, _16_bit_adder_4_s, _16_bit_adder_5_s,
       _16_bit_adder_6_s, _16_bit_adder_7_s, _16_bit_adder_8_s;

  _16_bit_adder _16_bit_adder_1 (.A(I), .B(16'hfff6), .S(_16_bit_adder_1_s));  // open: C
  _16_bit_adder _16_bit_adder_2 (.A(_16_bit_adder_1_s), .B(16'hfff6), .S(_16_bit_adder_2_s));  // open: C
  _16_bit_adder _16_bit_adder_3 (.A(_16_bit_adder_2_s), .B(16'hfff6), .S(_16_bit_adder_3_s));  // open: C
  _16_bit_adder _16_bit_adder_4 (.A(_16_bit_adder_3_s), .B(16'hfff6), .S(_16_bit_adder_4_s));  // open: C
  _16_bit_adder _16_bit_adder_5 (.A(_16_bit_adder_4_s), .B(16'hfff6), .S(_16_bit_adder_5_s));  // open: C
  _16_bit_adder _16_bit_adder_6 (.A(_16_bit_adder_5_s), .B(16'hfff6), .S(_16_bit_adder_6_s));  // open: C
  _16_bit_adder _16_bit_adder_7 (.A(_16_bit_adder_6_s), .B(16'hfff6), .S(_16_bit_adder_7_s));  // open: C
  _16_bit_adder _16_bit_adder_8 (.A(_16_bit_adder_7_s), .B(16'hfff6), .S(_16_bit_adder_8_s));  // open: C
  _16_bit_higher_than_9 _16_bit_higher_than_9_1 (.I(I), .O(_16_bit_higher_than_9_1_o));
  _16_bit_higher_than_9 _16_bit_higher_than_9_2 (.I(_16_bit_adder_1_s), .O(_16_bit_higher_than_9_2_o));
  _16_bit_higher_than_9 _16_bit_higher_than_9_3 (.I(_16_bit_adder_2_s), .O(_16_bit_higher_than_9_3_o));
  _16_bit_higher_than_9 _16_bit_higher_than_9_4 (.I(_16_bit_adder_3_s), .O(_16_bit_higher_than_9_4_o));
  _16_bit_higher_than_9 _16_bit_higher_than_9_5 (.I(_16_bit_adder_4_s), .O(_16_bit_higher_than_9_5_o));
  _16_bit_higher_than_9 _16_bit_higher_than_9_6 (.I(_16_bit_adder_5_s), .O(_16_bit_higher_than_9_6_o));
  _16_bit_higher_than_9 _16_bit_higher_than_9_7 (.I(_16_bit_adder_6_s), .O(_16_bit_higher_than_9_7_o));
  _16_bit_higher_than_9 _16_bit_higher_than_9_8 (.I(_16_bit_adder_7_s), .O(_16_bit_higher_than_9_8_o));
  _16_bit_higher_than_9 _16_bit_higher_than_9_9 (.I(_16_bit_adder_8_s), .O(_16_bit_higher_than_9_9_o));
  and and_1 (and_1_out, _16_bit_higher_than_9_1_o, ~_16_bit_higher_than_9_2_o);  // And
  and and_2 (and_2_out, _16_bit_higher_than_9_2_o, ~_16_bit_higher_than_9_3_o);  // And
  and and_3 (and_3_out, _16_bit_higher_than_9_3_o, ~_16_bit_higher_than_9_4_o);  // And
  and and_4 (and_4_out, _16_bit_higher_than_9_4_o, ~_16_bit_higher_than_9_5_o);  // And
  and and_5 (and_5_out, _16_bit_higher_than_9_5_o, ~_16_bit_higher_than_9_6_o);  // And
  and and_6 (and_6_out, _16_bit_higher_than_9_6_o, ~_16_bit_higher_than_9_7_o);  // And
  and and_7 (and_7_out, _16_bit_higher_than_9_7_o, ~_16_bit_higher_than_9_8_o);  // And
  and and_8 (and_8_out, _16_bit_higher_than_9_8_o, ~_16_bit_higher_than_9_9_o);  // And
  _1_to_4 _1_to_4_1 (.I(and_1_out), .O(_1_to_4_1_o));
  _1_to_4 _1_to_4_2 (.I(and_2_out), .O(_1_to_4_2_o));
  _1_to_4 _1_to_4_3 (.I(and_3_out), .O(_1_to_4_3_o));
  _1_to_4 _1_to_4_4 (.I(and_4_out), .O(_1_to_4_4_o));
  _1_to_4 _1_to_4_5 (.I(and_5_out), .O(_1_to_4_5_o));
  _1_to_4 _1_to_4_6 (.I(and_6_out), .O(_1_to_4_6_o));
  _1_to_4 _1_to_4_7 (.I(and_7_out), .O(_1_to_4_7_o));
  _1_to_4 _1_to_4_8 (.I(and_8_out), .O(_1_to_4_8_o));
  _1_to_4 _1_to_4_9 (.I(_16_bit_higher_than_9_9_o), .O(_1_to_4_9_o));
  assign and_9_out = _1_to_4_1_o & 4'b0001;  // And and_9, 4 bits wide
  assign and_10_out = _1_to_4_2_o & 4'b0010;  // And and_10, 4 bits wide
  assign and_11_out = _1_to_4_3_o & 4'b0011;  // And and_11, 4 bits wide
  assign and_12_out = _1_to_4_4_o & 4'b0100;  // And and_12, 4 bits wide
  assign and_13_out = _1_to_4_5_o & 4'b0101;  // And and_13, 4 bits wide
  assign and_14_out = _1_to_4_6_o & 4'b0110;  // And and_14, 4 bits wide
  assign and_15_out = _1_to_4_7_o & 4'b0111;  // And and_15, 4 bits wide
  assign and_16_out = _1_to_4_8_o & 4'b1000;  // And and_16, 4 bits wide
  assign and_17_out = _1_to_4_9_o & 4'b1001;  // And and_17, 4 bits wide
  assign or_1_out = and_9_out | and_10_out;  // Or or_1, 4 bits wide
  assign or_2_out = or_1_out | and_11_out;  // Or or_2, 4 bits wide
  assign or_3_out = or_2_out | and_12_out;  // Or or_3, 4 bits wide
  assign or_4_out = or_3_out | and_13_out;  // Or or_4, 4 bits wide
  assign or_5_out = or_4_out | and_14_out;  // Or or_5, 4 bits wide
  assign or_6_out = or_5_out | and_15_out;  // Or or_6, 4 bits wide
  assign or_7_out = or_6_out | and_16_out;  // Or or_7, 4 bits wide
  assign O = or_7_out | and_17_out;  // Or or_8, 4 bits wide
endmodule
