// Digital circuit 16_bit_higher_than_9.dig as structural Verilog
module _16_bit_higher_than_9 (
  input  [15:0] I,
  output O
);

  wire _4_bit_higher_than_9_1_o, or_1_out;

  _4_bit_higher_than_9 _4_bit_higher_than_9_1 (.I(I[3:0]), .O(_4_bit_higher_than_9_1_o));
  or or_1 (or_1_out, _4_bit_higher_than_9_1_o, I[4], I[5], I[6], I[7], I[8], I[9], I[10], I[11], I[12], I[13], I[14]);
  and and_1 (O, or_1_out, ~I[15]);  // And
endmodule
