// Digital circuit 16_bit_to_BCD.dig as structural Verilog
module _16_bit_to_BCD (
  input  [15:0] I,
  output [41:0] O
);

  wire bcd_7_sec_1_p2, bcd_7_sec_1_p3, bcd_7_sec_1_p4, bcd_7_sec_1_p5, bcd_7_sec_1_p6, bcd_7_sec_1_p7,
       bcd_7_sec_1_p8;

  // BCD_7_sec bcd_7_sec_1: pin names not known; wires that end beside it: I[3:0], bcd_7_sec_1_p2, bcd_7_sec_1_p3, bcd_7_sec_1_p4, bcd_7_sec_1_p5, bcd_7_sec_1_p6, bcd_7_sec_1_p7, bcd_7_sec_1_p8
  // _7_sec_to_connector _7_sec_to_connector_1: pin names not known; wires that end beside it: bcd_7_sec_1_p2, bcd_7_sec_1_p3, bcd_7_sec_1_p4, bcd_7_sec_1_p5, bcd_7_sec_1_p6, bcd_7_sec_1_p7, bcd_7_sec_1_p8, O[33:0]
  // Pins of 1 and 42 bits meet at O
endmodule
