// Digital circuit 2_bit_decoder.dig as structural Verilog
module _2_bit_decoder (
  input  [1:0] I,
  output [3:0] O
);

  and and_1 (O[0], ~I[0], ~I[1]);  // And
  and and_2 (O[1], I[0], ~I[1]);  // And
  and and_3 (O[2], ~I[0], I[1]);  // And
  and and_4 (O[3], I[0], I[1]);
endmodule
