// Digital circuit 2_bit_decoder_tester.dig as structural Verilog
module _2_bit_decoder_tester (
  input  [1:0] I,
  output [3:0] O
);

  wire [2:0] _2_bit_decoder_1_o;

  _2_bit_decoder _2_bit_decoder_1 (.I(I), .O({O[3], _2_bit_decoder_1_o}));
  or or_1 (O[0], _2_bit_decoder_1_o[0], _2_bit_decoder_1_o[1], _2_bit_decoder_1_o[2], O[3]);
  or or_2 (O[1], _2_bit_decoder_1_o[1], _2_bit_decoder_1_o[2], O[3]);
  or or_3 (O[2], _2_bit_decoder_1_o[2], O[3]);
endmodule
