// Digital circuit 2_bit_multiplexer.dig as structural Verilog
module _2_bit_multiplexer (
  input  [1:0] A1,
  input  [1:0] A2,
  input  S,
  output [1:0] O
);

  _1_bit_multiplexer _1_bit_multiplexer_1 (.A1(A1[0]), .A2(A2[0]), .S(S), .O(O[0]));
  _1_bit_multiplexer _1_bit_multiplexer_2 (.A1(A1[1]), .A2(A2[1]), .S(S), .O(O[1]));
endmodule
