// Digital circuit 3_bit_decoder.dig as structural Verilog
module _3_bit_decoder (
  input  [2:0] I,
  output [7:0] O
);

  wire [3:0] _2_bit_decoder_1_o;

  _2_bit_decoder _2_bit_decoder_1 (.I(I[1:0]), .O(_2_bit_decoder_1_o));
  assign O[3:0] = _2_bit_decoder_1_o & ~{4{I[2]}};  // And and_1, 4 bits wide
  assign O[7:4] = _2_bit_decoder_1_o & {4{I[2]}};  // And and_2, 4 bits wide
endmodule
