// Digital circuit 3_bit_decoder_tester.dig as structural Verilog
module _3_bit_decoder_tester (
  input  [2:0] I
);

  wire [7:0] _3_bit_decoder_1_o;

  _3_bit_decoder _3_bit_decoder_1 (.I(I), .O(_3_bit_decoder_1_o));
endmodule
