// Digital circuit 4_bit_decoder.dig as structural Verilog
module _4_bit_decoder (
  input  [3:0] I,
  output [15:0] O
);

  wire [3:0] _2_bit_decoder_1_o;
  wire [3:3] and_1_out, and_2_out, and_3_out, and_4_out;

  _2_bit_decoder _2_bit_decoder_1 (.I(I[1:0]), .O(_2_bit_decoder_1_o));
  and and_1 (and_1_out[3], ~I[2], ~I[3]);  // And
  and and_2 (and_2_out[3], I[2], ~I[3]);  // And
  and and_3 (and_3_out[3], ~I[2], I[3]);  // And
  and and_4 (and_4_out[3], I[2], I[3]);
  assign O[3:0] = _2_bit_decoder_1_o & {4{and_1_out[3]}};  // And and_5, 4 bits wide
  assign O[7:4] = _2_bit_decoder_1_o & {4{and_2_out[3]}};  // And and_6, 4 bits wide
  assign O[11:8] = _2_bit_decoder_1_o & {4{and_3_out[3]}};  // And and_7, 4 bits wide
  assign O[15:12] = _2_bit_decoder_1_o & {4{and_4_out[3]}};  // And and_8, 4 bits wide
endmodule
