// Digital circuit 4_bit_decoder_and_lower.dig as structural Verilog
module _4_bit_decoder_and_lower (
  input  [3:0] I,
  output [15:0] _0
);

  wire [14:0] _4_bit_decoder_1_o;

  _4_bit_decoder _4_bit_decoder_1 (.I(I), .O({_0[15], _4_bit_decoder_1_o}));
  or or_1 (_0[14], _4_bit_decoder_1_o[14], _0[15]);
  or or_2 (_0[13], _4_bit_decoder_1_o[13], _0[14]);
  or or_3 (_0[12], _4_bit_decoder_1_o[12], _0[13]);
  or or_4 (_0[11], _4_bit_decoder_1_o[11], _0[12]);
  or or_5 (_0[10], _4_bit_decoder_1_o[10], _0[11]);
  or or_6 (_0[9], _4_bit_decoder_1_o[9], _0[10]);
  or or_7 (_0[8], _4_bit_decoder_1_o[8], _0[9]);
  or or_8 (_0[7], _4_bit_decoder_1_o[7], _0[8]);
  or or_9 (_0[6], _4_bit_decoder_1_o[6], _0[7]);
  or or_10 (_0[5], _4_bit_decoder_1_o[5], _0[6]);
  or or_11 (_0[4], _4_bit_decoder_1_o[4], _0[5]);
  or or_12 (_0[3], _4_bit_decoder_1_o[3], _0[4]);
  or or_13 (_0[2], _4_bit_decoder_1_o[2], _0[3]);
  or or_14 (_0[1], _4_bit_decoder_1_o[1], _0[2]);
  or or_15 (_0[0], _4_bit_decoder_1_o[0], _0[1]);
endmodule
