// Digital circuit 4_bit_decoder_tester.dig as structural Verilog
module _4_bit_decoder_tester (
  input  [3:0] I
);

  wire [15:0] _4_bit_decoder_1_o;

  _4_bit_decoder _4_bit_decoder_1 (.I(I), .O(_4_bit_decoder_1_o));
endmodule
