// Digital circuit 4_bit_higher_than_9.dig as structural Verilog
module _4_bit_higher_than_9 (
  input  [3:0] I,
  output O
);

  wire and_1_out, and_2_out, or_1_out;

  and and_1 (and_1_out, ~I[0], ~I[1], ~I[2]);  // And
  and and_2 (and_2_out, I[0], ~I[1], ~I[2]);  // And
  or or_1 (or_1_out, and_1_out, and_2_out);
  and and_3 (O, ~or_1_out, I[3]);  // And
endmodule
