// Digital circuit 4_bit_multiplexer.dig as structural Verilog
module _4_bit_multiplexer (
  input  [3:0] A1,
  input  [3:0] A2,
  input  S,
  output [3:0] O
);

  _2_bit_multiplexer _2_bit_multiplexer_1 (.A1(A1[1:0]), .A2(A2[1:0]), .S(S), .O(O[1:0]));
  _2_bit_multiplexer _2_bit_multiplexer_2 (.A1(A1[3:2]), .A2(A2[3:2]), .S(S), .O(O[3:2]));
endmodule
