// Digital circuit 8_bit_adder.dig as structural Verilog
module _8_bit_adder (
  input  [7:0] A,
  input  [7:0] B,
  output [7:0] S,
  output C
);

  wire _4_bit_carry_ripple_adder_1_c_out;

  _4_bit_carry_ripple_adder _4_bit_carry_ripple_adder_1 (
    .A(A[3:0]), .B(B[3:0]), .C_in(1'b0), .S(S[3:0]), .C_out(_4_bit_carry_ripple_adder_1_c_out));
  _4_bit_carry_select_adder _4_bit_carry_select_adder_1 (
    .A(A[7:4]), .B(B[7:4]), .C_in(_4_bit_carry_ripple_adder_1_c_out), .S(S[7:4]), .C_out(C));
endmodule
