// Digital circuit 8_bit_alu.dig as structural Verilog
module _8_bit_alu (
  input  [7:0] A,
  input  [7:0] B,
  input  [2:0] O,
  output [7:0] Y
);

  wire [7:0] _8_bit_adder_1_s, _8_bit_adder_2_s, _8_bit_adder_3_s, or_1_out, shift_8_bit_by_8_1_y,
       shift_8_bit_by_8_2_y, shift_8_bit_by_8_3_y, shift_8_bit_by_8_4_y;

  shift_8_bit_by_8 shift_8_bit_by_8_1 (.A(A), .B(B), .O(1'b0), .Y(shift_8_bit_by_8_1_y));
  shift_8_bit_by_8 shift_8_bit_by_8_2 (.A(A), .B(B), .O(1'b1), .Y(shift_8_bit_by_8_2_y));
  shift_8_bit_by_8 shift_8_bit_by_8_3 (.A(A), .B(8'h1), .O(1'b0), .Y(shift_8_bit_by_8_3_y));
  shift_8_bit_by_8 shift_8_bit_by_8_4 (.A(B), .B(8'h4), .O(1'b0), .Y(shift_8_bit_by_8_4_y));
  _8_bit_adder _8_bit_adder_1 (.A(A), .B(B), .S(_8_bit_adder_1_s));  // open: C
  _8_bit_adder _8_bit_adder_2 (.A(A), .B(8'h1), .S(_8_bit_adder_2_s));  // open: C
  _8_bit_adder _8_bit_adder_3 (.A(A), .B({8{1'b1}}), .S(_8_bit_adder_3_s));  // open: C
  assign or_1_out = A | shift_8_bit_by_8_4_y;  // Or or_1, 8 bits wide
  _8_bit_3_bit_multiplexer _8_bit_3_bit_multiplexer_1 (
    .S(O), .A1(shift_8_bit_by_8_1_y), .A2(shift_8_bit_by_8_2_y), .A3(shift_8_bit_by_8_3_y), .A4(or_1_out),
    .A5(_8_bit_adder_1_s), .A6(_8_bit_adder_2_s), .A7(_8_bit_adder_3_s), .A8(8'hd), .O(Y));

  // Notes on the sheet:
  //   A << B
  //   A >> B
  //   A << 1
  //   _*
  //   A + B
  //   A + 1
  //   A - 1
  //   13_10
endmodule
