// Digital circuit 8_bit_multiplexer.dig as structural Verilog
module _8_bit_multiplexer (
  input  [7:0] A1,
  input  [7:0] A2,
  input  S,
  output [7:0] O
);

  _4_bit_multiplexer _4_bit_multiplexer_1 (.A1(A1[3:0]), .A2(A2[3:0]), .S(S), .O(O[3:0]));
  _4_bit_multiplexer _4_bit_multiplexer_2 (.A1(A1[7:4]), .A2(A2[7:4]), .S(S), .O(O[7:4]));
endmodule
