// Digital circuit BCD_7_sec_tester.dig as structural Verilog
module BCD_7_sec_tester (
  input  [3:0] in_1
);

  wire bcd_7_sec_1_p2, bcd_7_sec_1_p3, bcd_7_sec_1_p4, bcd_7_sec_1_p5, bcd_7_sec_1_p6, bcd_7_sec_1_p7,
       bcd_7_sec_1_p8;
  wire [3:0] _7_sec_to_connector_1_p8;
  wire [6:4] _7_sec_to_connector_1_p8_2;

  // BCD_7_sec bcd_7_sec_1: pin names not known; wires that end beside it: in_1, bcd_7_sec_1_p2, bcd_7_sec_1_p3, bcd_7_sec_1_p4, bcd_7_sec_1_p5, bcd_7_sec_1_p6, bcd_7_sec_1_p7, bcd_7_sec_1_p8
  Seven_Seg seven_seg_1 (
    .a(bcd_7_sec_1_p2), .b(bcd_7_sec_1_p3), .c(bcd_7_sec_1_p4), .d(bcd_7_sec_1_p5), .e(bcd_7_sec_1_p6),
    .f(bcd_7_sec_1_p7), .g(bcd_7_sec_1_p8), .dp(1'b0));
  // _7_sec_to_connector _7_sec_to_connector_1: pin names not known; wires that end beside it: bcd_7_sec_1_p2, bcd_7_sec_1_p3, bcd_7_sec_1_p4, bcd_7_sec_1_p5, bcd_7_sec_1_p6, bcd_7_sec_1_p7, bcd_7_sec_1_p8, {_7_sec_to_connector_1_p8_2, _7_sec_to_connector_1_p8}
  Seven_Seg seven_seg_2 (
    .a(_7_sec_to_connector_1_p8[3]), .b(_7_sec_to_connector_1_p8[2]), .c(_7_sec_to_connector_1_p8[1]),
    .d(_7_sec_to_connector_1_p8[0]), .e(_7_sec_to_connector_1_p8_2[4]), .f(_7_sec_to_connector_1_p8_2[5]),
    .g(_7_sec_to_connector_1_p8_2[6]), .dp(1'b0));
  Seven_Seg seven_seg_3 (
    .a(_7_sec_to_connector_1_p8[3]), .b(_7_sec_to_connector_1_p8[2]), .c(_7_sec_to_connector_1_p8[1]),
    .d(_7_sec_to_connector_1_p8[0]), .e(_7_sec_to_connector_1_p8_2[4]), .f(_7_sec_to_connector_1_p8_2[5]),
    .g(_7_sec_to_connector_1_p8_2[6]), .dp(1'b0));
endmodule
