// Digital circuit final_adder.dig as structural Verilog
module final_adder (
  input  [7:0] A,
  input  [7:0] B,
  output [7:0] S,
  output C
);

  wire _3_bit_carry_ripple_adder_1_c_out;

  _3_bit_carry_ripple_adder _3_bit_carry_ripple_adder_1 (
    .A(A[2:0]), .B(B[2:0]), .C_in(1'b0), .S(S[2:0]), .C_out(_3_bit_carry_ripple_adder_1_c_out));
  _5_bit_carry_select_adder _5_bit_carry_select_adder_1 (
    .A(A[7:3]), .B(B[7:3]), .C_in(_3_bit_carry_ripple_adder_1_c_out), .S(S[7:3]), .C_out(C));
endmodule
