// Digital circuit final_adder_tester.dig as structural Verilog
module final_adder_tester (
  input  [7:0] A,
  input  [7:0] B
);

  wire [3:0] final_adder_1_p3, final_adder_1_p3_2;

  // final_adder final_adder_1: pin names not known; wires that end beside it: A, B, {final_adder_1_p3_2, final_adder_1_p3}
  Seven_Seg_Hex seven_seg_hex_1 (.d(final_adder_1_p3_2), .dp(1'b0));
  Seven_Seg_Hex seven_seg_hex_2 (.d(final_adder_1_p3), .dp(1'b0));
endmodule
