// Digital circuit shift_8_bit_by_8_tester.dig as structural Verilog
module shift_8_bit_by_8_tester (
  input  [7:0] A,
  input  [7:0] B,
  input  O
);

  wire [7:0] shift_8_bit_by_8_1_y;

  shift_8_bit_by_8 shift_8_bit_by_8_1 (.A(A), .B(B), .O(O), .Y(shift_8_bit_by_8_1_y));
endmodule
