// Digital circuit two_compliment_to_singed_number.dig as structural Verilog
module two_compliment_to_singed_number (
  input  [15:0] I,
  output [15:0] O,
  output S
);

  wire [15:0] _16_bit_adder_1_s, not_1_out;

  assign not_1_out = ~I;  // Not not_1, 16 bits wide
  _16_bit_adder _16_bit_adder_1 (.A(not_1_out), .B(16'h1), .S(_16_bit_adder_1_s));  // open: C
  _16_bit_multiplexer _16_bit_multiplexer_1 (.A1(I), .A2(_16_bit_adder_1_s), .S(I[15]), .O(O));

  assign S = I[15];
endmodule
