// Digital circuit 16_bit_adder.dig as structural Verilog
module _16_bit_adder (
  input  [15:0] A,
  input  [15:0] B,
  output [15:0] S,
  output C
);

  wire _4_bit_carry_ripple_adder_1_c_out, _4_bit_carry_select_adder_1_c_out,
       _4_bit_carry_select_adder_2_c_out;

  _4_bit_carry_ripple_adder _4_bit_carry_ripple_adder_1 (
    .A(A[3:0]), .B(B[3:0]), .C_in(1'b0), .S(S[3:0]), .C_out(_4_bit_carry_ripple_adder_1_c_out));
  _4_bit_carry_select_adder _4_bit_carry_select_adder_1 (
    .A(A[7:4]), .B(B[7:4]), .C_in(_4_bit_carry_ripple_adder_1_c_out), .S(S[7:4]),
    .C_out(_4_bit_carry_select_adder_1_c_out));
  _4_bit_carry_select_adder _4_bit_carry_select_adder_2 (
    .A(A[11:8]), .B(B[11:8]), .C_in(_4_bit_carry_select_adder_1_c_out), .S(S[11:8]),
    .C_out(_4_bit_carry_select_adder_2_c_out));
  _4_bit_carry_select_adder _4_bit_carry_select_adder_3 (
    .A(A[15:12]), .B(B[15:12]), .C_in(_4_bit_carry_select_adder_2_c_out), .S(S[15:12]), .C_out(C));

  // Notes on the sheet:
  //   4-bit carry select adders with Input A and B split by four, so each two 4bits
  //   are input to a 4bit carry select adder.
endmodule
