// Digital circuit 16_bit_hex_to_BCD.dig as structural Verilog
module _16_bit_hex_to_BCD (
  input  [15:0] I,
  output [3:0] D_1,
  output [3:0] D_2,
  output [3:0] D_3,
  output [3:0] D_4,
  output [3:0] D_5
);

  wire to_bcd_block_1_o_1, to_bcd_block_1_o_2, to_bcd_block_1_o_3, to_bcd_block_1_o_4, to_bcd_block_2_o_1,
       to_bcd_block_2_o_2, to_bcd_block_2_o_3, to_bcd_block_2_o_4, to_bcd_block_3_o_1, to_bcd_block_3_o_2,
       to_bcd_block_3_o_3, to_bcd_block_3_o_4, to_bcd_block_4_o_1, to_bcd_block_4_o_2, to_bcd_block_4_o_3,
       to_bcd_block_4_o_4, to_bcd_block_5_o_1, to_bcd_block_5_o_2, to_bcd_block_5_o_3, to_bcd_block_5_o_4,
       to_bcd_block_6_o_1, to_bcd_block_6_o_2, to_bcd_block_6_o_3, to_bcd_block_6_o_4, to_bcd_block_7_o_1,
       to_bcd_block_7_o_2, to_bcd_block_7_o_3, to_bcd_block_7_o_4, to_bcd_block_8_o_1, to_bcd_block_8_o_2,
       to_bcd_block_8_o_3, to_bcd_block_8_o_4, to_bcd_block_9_o_1, to_bcd_block_9_o_2, to_bcd_block_9_o_3,
       to_bcd_block_9_o_4, to_bcd_block_10_o_1, to_bcd_block_10_o_2, to_bcd_block_10_o_3,
       to_bcd_block_10_o_4, to_bcd_block_11_o_1, to_bcd_block_11_o_2, to_bcd_block_11_o_3,
       to_bcd_block_11_o_4, to_bcd_block_12_o_1, to_bcd_block_12_o_2, to_bcd_block_12_o_3,
       to_bcd_block_12_o_4, to_bcd_block_13_o_1, to_bcd_block_13_o_2, to_bcd_block_13_o_3,
       to_bcd_block_13_o_4, to_bcd_block_14_o_1, to_bcd_block_14_o_2, to_bcd_block_14_o_3,
       to_bcd_block_14_o_4, to_bcd_block_15_o_1, to_bcd_block_15_o_2, to_bcd_block_15_o_3,
       to_bcd_block_15_o_4, to_bcd_block_16_o_1, to_bcd_block_16_o_2, to_bcd_block_16_o_3,
       to_bcd_block_16_o_4, to_bcd_block_17_o_1, to_bcd_block_17_o_2, to_bcd_block_17_o_3,
       to_bcd_block_17_o_4, to_bcd_block_18_o_1, to_bcd_block_18_o_2, to_bcd_block_18_o_3,
       to_bcd_block_18_o_4, to_bcd_block_19_o_1, to_bcd_block_19_o_2, to_bcd_block_19_o_3,
       to_bcd_block_19_o_4, to_bcd_block_20_o_1, to_bcd_block_20_o_2, to_bcd_block_20_o_3,
       to_bcd_block_20_o_4, to_bcd_block_21_o_1, to_bcd_block_21_o_2, to_bcd_block_21_o_3,
       to_bcd_block_21_o_4, to_bcd_block_22_o_1, to_bcd_block_22_o_2, to_bcd_block_22_o_3,
       to_bcd_block_23_o_1, to_bcd_block_23_o_2, to_bcd_block_23_o_3, to_bcd_block_23_o_4,
       to_bcd_block_24_o_1, to_bcd_block_24_o_2, to_bcd_block_24_o_3, to_bcd_block_24_o_4,
       to_bcd_block_25_o_1, to_bcd_block_25_o_2, to_bcd_block_25_o_3, to_bcd_block_25_o_4,
       to_bcd_block_26_o_1, to_bcd_block_26_o_2, to_bcd_block_26_o_3, to_bcd_block_27_o_1,
       to_bcd_block_27_o_2, to_bcd_block_27_o_3, to_bcd_block_27_o_4, to_bcd_block_28_o_1,
       to_bcd_block_28_o_2, to_bcd_block_28_o_3, to_bcd_block_28_o_4, to_bcd_block_29_o_1,
       to_bcd_block_29_o_2, to_bcd_block_29_o_3, to_bcd_block_29_o_4, to_bcd_block_30_o_1,
       to_bcd_block_30_o_2, to_bcd_block_30_o_3;

  to_BCD_block to_bcd_block_1 (
    .x_1(I[13]), .x_2(I[14]), .x_3(I[15]), .x_4(1'b0), .o_1(to_bcd_block_1_o_1), .o_2(to_bcd_block_1_o_2),
    .o_3(to_bcd_block_1_o_3), .o_4(to_bcd_block_1_o_4));
  to_BCD_block to_bcd_block_2 (
    .x_1(I[12]), .x_2(to_bcd_block_1_o_1), .x_3(to_bcd_block_1_o_2), .x_4(to_bcd_block_1_o_3),
    .o_1(to_bcd_block_2_o_1), .o_2(to_bcd_block_2_o_2), .o_3(to_bcd_block_2_o_3), .o_4(to_bcd_block_2_o_4));
  to_BCD_block to_bcd_block_3 (
    .x_1(I[11]), .x_2(to_bcd_block_2_o_1), .x_3(to_bcd_block_2_o_2), .x_4(to_bcd_block_2_o_3),
    .o_1(to_bcd_block_3_o_1), .o_2(to_bcd_block_3_o_2), .o_3(to_bcd_block_3_o_3), .o_4(to_bcd_block_3_o_4));
  to_BCD_block to_bcd_block_4 (
    .x_1(I[10]), .x_2(to_bcd_block_3_o_1), .x_3(to_bcd_block_3_o_2), .x_4(to_bcd_block_3_o_3),
    .o_1(to_bcd_block_4_o_1), .o_2(to_bcd_block_4_o_2), .o_3(to_bcd_block_4_o_3), .o_4(to_bcd_block_4_o_4));
  to_BCD_block to_bcd_block_5 (
    .x_1(to_bcd_block_3_o_4), .x_2(to_bcd_block_2_o_4), .x_3(to_bcd_block_1_o_4), .x_4(1'b0),
    .o_1(to_bcd_block_5_o_1), .o_2(to_bcd_block_5_o_2), .o_3(to_bcd_block_5_o_3), .o_4(to_bcd_block_5_o_4));
  to_BCD_block to_bcd_block_6 (
    .x_1(I[9]), .x_2(to_bcd_block_4_o_1), .x_3(to_bcd_block_4_o_2), .x_4(to_bcd_block_4_o_3),
    .o_1(to_bcd_block_6_o_1), .o_2(to_bcd_block_6_o_2), .o_3(to_bcd_block_6_o_3), .o_4(to_bcd_block_6_o_4));
  to_BCD_block to_bcd_block_7 (
    .x_1(to_bcd_block_4_o_4), .x_2(to_bcd_block_5_o_1), .x_3(to_bcd_block_5_o_2), .x_4(to_bcd_block_5_o_3),
    .o_1(to_bcd_block_7_o_1), .o_2(to_bcd_block_7_o_2), .o_3(to_bcd_block_7_o_3), .o_4(to_bcd_block_7_o_4));
  to_BCD_block to_bcd_block_8 (
    .x_1(I[8]), .x_2(to_bcd_block_6_o_1), .x_3(to_bcd_block_6_o_2), .x_4(to_bcd_block_6_o_3),
    .o_1(to_bcd_block_8_o_1), .o_2(to_bcd_block_8_o_2), .o_3(to_bcd_block_8_o_3), .o_4(to_bcd_block_8_o_4));
  to_BCD_block to_bcd_block_9 (
    .x_1(to_bcd_block_6_o_4), .x_2(to_bcd_block_7_o_1), .x_3(to_bcd_block_7_o_2), .x_4(to_bcd_block_7_o_3),
    .o_1(to_bcd_block_9_o_1), .o_2(to_bcd_block_9_o_2), .o_3(to_bcd_block_9_o_3), .o_4(to_bcd_block_9_o_4));
  to_BCD_block to_bcd_block_10 (
    .x_1(I[7]), .x_2(to_bcd_block_8_o_1), .x_3(to_bcd_block_8_o_2), .x_4(to_bcd_block_8_o_3),
    .o_1(to_bcd_block_10_o_1), .o_2(to_bcd_block_10_o_2), .o_3(to_bcd_block_10_o_3), .o_4(to_bcd_block_10_o_4));
  to_BCD_block to_bcd_block_11 (
    .x_1(to_bcd_block_8_o_4), .x_2(to_bcd_block_9_o_1), .x_3(to_bcd_block_9_o_2), .x_4(to_bcd_block_9_o_3),
    .o_1(to_bcd_block_11_o_1), .o_2(to_bcd_block_11_o_2), .o_3(to_bcd_block_11_o_3), .o_4(to_bcd_block_11_o_4));
  to_BCD_block to_bcd_block_12 (
    .x_1(to_bcd_block_9_o_4), .x_2(to_bcd_block_7_o_4), .x_3(to_bcd_block_5_o_4), .x_4(1'b0),
    .o_1(to_bcd_block_12_o_1), .o_2(to_bcd_block_12_o_2), .o_3(to_bcd_block_12_o_3), .o_4(to_bcd_block_12_o_4));
  to_BCD_block to_bcd_block_13 (
    .x_1(I[6]), .x_2(to_bcd_block_10_o_1), .x_3(to_bcd_block_10_o_2), .x_4(to_bcd_block_10_o_3),
    .o_1(to_bcd_block_13_o_1), .o_2(to_bcd_block_13_o_2), .o_3(to_bcd_block_13_o_3), .o_4(to_bcd_block_13_o_4));
  to_BCD_block to_bcd_block_14 (
    .x_1(to_bcd_block_10_o_4), .x_2(to_bcd_block_11_o_1), .x_3(to_bcd_block_11_o_2),
    .x_4(to_bcd_block_11_o_3), .o_1(to_bcd_block_14_o_1), .o_2(to_bcd_block_14_o_2),
    .o_3(to_bcd_block_14_o_3), .o_4(to_bcd_block_14_o_4));
  to_BCD_block to_bcd_block_15 (
    .x_1(to_bcd_block_11_o_4), .x_2(to_bcd_block_12_o_1), .x_3(to_bcd_block_12_o_2),
    .x_4(to_bcd_block_12_o_3), .o_1(to_bcd_block_15_o_1), .o_2(to_bcd_block_15_o_2),
    .o_3(to_bcd_block_15_o_3), .o_4(to_bcd_block_15_o_4));
  to_BCD_block to_bcd_block_16 (
    .x_1(I[5]), .x_2(to_bcd_block_13_o_1), .x_3(to_bcd_block_13_o_2), .x_4(to_bcd_block_13_o_3),
    .o_1(to_bcd_block_16_o_1), .o_2(to_bcd_block_16_o_2), .o_3(to_bcd_block_16_o_3), .o_4(to_bcd_block_16_o_4));
  to_BCD_block to_bcd_block_17 (
    .x_1(to_bcd_block_13_o_4), .x_2(to_bcd_block_14_o_1), .x_3(to_bcd_block_14_o_2),
    .x_4(to_bcd_block_14_o_3), .o_1(to_bcd_block_17_o_1), .o_2(to_bcd_block_17_o_2),
    .o_3(to_bcd_block_17_o_3), .o_4(to_bcd_block_17_o_4));
  to_BCD_block to_bcd_block_18 (
    .x_1(to_bcd_block_14_o_4), .x_2(to_bcd_block_15_o_1), .x_3(to_bcd_block_15_o_2),
    .x_4(to_bcd_block_15_o_3), .o_1(to_bcd_block_18_o_1), .o_2(to_bcd_block_18_o_2),
    .o_3(to_bcd_block_18_o_3), .o_4(to_bcd_block_18_o_4));
  to_BCD_block to_bcd_block_19 (
    .x_1(I[4]), .x_2(to_bcd_block_16_o_1), .x_3(to_bcd_block_16_o_2), .x_4(to_bcd_block_16_o_3),
    .o_1(to_bcd_block_19_o_1), .o_2(to_bcd_block_19_o_2), .o_3(to_bcd_block_19_o_3), .o_4(to_bcd_block_19_o_4));
  to_BCD_block to_bcd_block_20 (
    .x_1(to_bcd_block_16_o_4), .x_2(to_bcd_block_17_o_1), .x_3(to_bcd_block_17_o_2),
    .x_4(to_bcd_block_17_o_3), .o_1(to_bcd_block_20_o_1), .o_2(to_bcd_block_20_o_2),
    .o_3(to_bcd_block_20_o_3), .o_4(to_bcd_block_20_o_4));
  to_BCD_block to_bcd_block_21 (
    .x_1(to_bcd_block_17_o_4), .x_2(to_bcd_block_18_o_1), .x_3(to_bcd_block_18_o_2),
    .x_4(to_bcd_block_18_o_3), .o_1(to_bcd_block_21_o_1), .o_2(to_bcd_block_21_o_2),
    .o_3(to_bcd_block_21_o_3), .o_4(to_bcd_block_21_o_4));
  to_BCD_block to_bcd_block_22 (
    .x_1(to_bcd_block_18_o_4), .x_2(to_bcd_block_15_o_4), .x_3(to_bcd_block_12_o_4), .x_4(1'b0),
    .o_1(to_bcd_block_22_o_1), .o_2(to_bcd_block_22_o_2), .o_3(to_bcd_block_22_o_3), .o_4(D_5[3]));
  to_BCD_block to_bcd_block_23 (
    .x_1(I[3]), .x_2(to_bcd_block_19_o_1), .x_3(to_bcd_block_19_o_2), .x_4(to_bcd_block_19_o_3),
    .o_1(to_bcd_block_23_o_1), .o_2(to_bcd_block_23_o_2), .o_3(to_bcd_block_23_o_3), .o_4(to_bcd_block_23_o_4));
  to_BCD_block to_bcd_block_24 (
    .x_1(to_bcd_block_19_o_4), .x_2(to_bcd_block_20_o_1), .x_3(to_bcd_block_20_o_2),
    .x_4(to_bcd_block_20_o_3), .o_1(to_bcd_block_24_o_1), .o_2(to_bcd_block_24_o_2),
    .o_3(to_bcd_block_24_o_3), .o_4(to_bcd_block_24_o_4));
  to_BCD_block to_bcd_block_25 (
    .x_1(to_bcd_block_20_o_4), .x_2(to_bcd_block_21_o_1), .x_3(to_bcd_block_21_o_2),
    .x_4(to_bcd_block_21_o_3), .o_1(to_bcd_block_25_o_1), .o_2(to_bcd_block_25_o_2),
    .o_3(to_bcd_block_25_o_3), .o_4(to_bcd_block_25_o_4));
  to_BCD_block to_bcd_block_26 (
    .x_1(to_bcd_block_21_o_4), .x_2(to_bcd_block_22_o_1), .x_3(to_bcd_block_22_o_2),
    .x_4(to_bcd_block_22_o_3), .o_1(to_bcd_block_26_o_1), .o_2(to_bcd_block_26_o_2),
    .o_3(to_bcd_block_26_o_3), .o_4(D_5[2]));
  to_BCD_block to_bcd_block_27 (
    .x_1(I[2]), .x_2(to_bcd_block_23_o_1), .x_3(to_bcd_block_23_o_2), .x_4(to_bcd_block_23_o_3),
    .o_1(to_bcd_block_27_o_1), .o_2(to_bcd_block_27_o_2), .o_3(to_bcd_block_27_o_3), .o_4(to_bcd_block_27_o_4));
  to_BCD_block to_bcd_block_28 (
    .x_1(to_bcd_block_23_o_4), .x_2(to_bcd_block_24_o_1), .x_3(to_bcd_block_24_o_2),
    .x_4(to_bcd_block_24_o_3), .o_1(to_bcd_block_28_o_1), .o_2(to_bcd_block_28_o_2),
    .o_3(to_bcd_block_28_o_3), .o_4(to_bcd_block_28_o_4));
  to_BCD_block to_bcd_block_29 (
    .x_1(to_bcd_block_24_o_4), .x_2(to_bcd_block_25_o_1), .x_3(to_bcd_block_25_o_2),
    .x_4(to_bcd_block_25_o_3), .o_1(to_bcd_block_29_o_1), .o_2(to_bcd_block_29_o_2),
    .o_3(to_bcd_block_29_o_3), .o_4(to_bcd_block_29_o_4));
  to_BCD_block to_bcd_block_30 (
    .x_1(to_bcd_block_25_o_4), .x_2(to_bcd_block_26_o_1), .x_3(to_bcd_block_26_o_2),
    .x_4(to_bcd_block_26_o_3), .o_1(to_bcd_block_30_o_1), .o_2(to_bcd_block_30_o_2),
    .o_3(to_bcd_block_30_o_3), .o_4(D_5[1]));
  to_BCD_block to_bcd_block_31 (
    .x_1(I[1]), .x_2(to_bcd_block_27_o_1), .x_3(to_bcd_block_27_o_2), .x_4(to_bcd_block_27_o_3),
    .o_1(D_1[1]), .o_2(D_1[2]), .o_3(D_1[3]), .o_4(D_2[0]));
  to_BCD_block to_bcd_block_32 (
    .x_1(to_bcd_block_27_o_4), .x_2(to_bcd_block_28_o_1), .x_3(to_bcd_block_28_o_2),
    .x_4(to_bcd_block_28_o_3), .o_1(D_2[1]), .o_2(D_2[2]), .o_3(D_2[3]), .o_4(D_3[0]));
  to_BCD_block to_bcd_block_33 (
    .x_1(to_bcd_block_28_o_4), .x_2(to_bcd_block_29_o_1), .x_3(to_bcd_block_29_o_2),
    .x_4(to_bcd_block_29_o_3), .o_1(D_3[1]), .o_2(D_3[2]), .o_3(D_3[3]), .o_4(D_4[0]));
  to_BCD_block to_bcd_block_34 (
    .x_1(to_bcd_block_29_o_4), .x_2(to_bcd_block_30_o_1), .x_3(to_bcd_block_30_o_2),
    .x_4(to_bcd_block_30_o_3), .o_1(D_4[1]), .o_2(D_4[2]), .o_3(D_4[3]), .o_4(D_5[0]));

  assign D_1[0] = I[0];

  // Notes on the sheet:
  //   the 16 bit digit will have each of its 4bit blocks turned into a BCD.
  //   the interconnection between the to_BCD_blocks ensures, that the
  //   16bit number is accurately distributed across the decimal, since each
  //   digit position relies on the one before it.
endmodule
