// Digital circuit 16_bit_multiplexer.dig as structural Verilog
module _16_bit_multiplexer (
  input  [15:0] A1,
  input  [15:0] A2,
  input  S,
  output [15:0] O
);

  _8_bit_multiplexer _8_bit_multiplexer_1 (.A1(A1[7:0]), .A2(A2[7:0]), .S(S), .O(O[7:0]));
  _8_bit_multiplexer _8_bit_multiplexer_2 (.A1(A1[15:8]), .A2(A2[15:8]), .S(S), .O(O[15:8]));

  // Notes on the sheet:
  //   two 8 bit multiplexers connected
  //   through one deciding Input S and
  //   giving out the concatenated Outputs
  //   so that they can be 16bit long.
endmodule
