// Digital circuit 16_bit_to_6_7_seg_connector.dig as structural Verilog
module _16_bit_to_6_7_seg_connector (
  input  [7:0] A,
  input  [7:0] B,
  output [41:0] O
);

  wire _4_bit_equal_0_1_o, _4_bit_equal_0_2_o, _4_bit_equal_0_3_o, _4_bit_equal_0_4_o,
       _7_bit_multiplexer_1_p4, _7_bit_multiplexer_2_p4, _7_bit_multiplexer_3_p4, _7_bit_multiplexer_4_p4,
       _7_bit_multiplexer_5_p4, _7_bit_multiplexer_6_p4, _7_bit_multiplexer_7_p4, _7_bit_multiplexer_8_p4,
       _7_bit_multiplexer_9_p4, and_1_out, and_2_out, and_3_out, and_4_out, and_5_out, and_6_out, and_7_out,
       and_8_out, and_9_out, and_10_out, and_11_out, bcd_7_seg_1_o, bcd_7_seg_2_p2, bcd_7_seg_3_p2,
       bcd_7_seg_4_p2, bcd_7_seg_5_p2, two_compliment_to_singed_number_1_s;
  wire [3:0] _16_bit_hex_to_bcd_1_d_1, _16_bit_hex_to_bcd_1_d_2, _16_bit_hex_to_bcd_1_d_3,
       _16_bit_hex_to_bcd_1_d_4, _16_bit_hex_to_bcd_1_d_5;
  wire [15:0] two_compliment_to_singed_number_1_o;

  two_compliment_to_singed_number two_compliment_to_singed_number_1 (
    .I({B, A}), .O(two_compliment_to_singed_number_1_o), .S(two_compliment_to_singed_number_1_s));
  _16_bit_hex_to_BCD _16_bit_hex_to_bcd_1 (
    .I(two_compliment_to_singed_number_1_o), .D_1(_16_bit_hex_to_bcd_1_d_1), .D_2(_16_bit_hex_to_bcd_1_d_2),
    .D_3(_16_bit_hex_to_bcd_1_d_3), .D_4(_16_bit_hex_to_bcd_1_d_4), .D_5(_16_bit_hex_to_bcd_1_d_5));
  BCD_7_seg bcd_7_seg_1 (.I(_16_bit_hex_to_bcd_1_d_1), .O(bcd_7_seg_1_o));
  // BCD_7_seg bcd_7_seg_2: pin names not known; wires that end beside it: _16_bit_hex_to_bcd_1_d_2, bcd_7_seg_2_p2
  _4_bit_equal_0 _4_bit_equal_0_1 (.I(_16_bit_hex_to_bcd_1_d_2), .O(_4_bit_equal_0_1_o));
  // BCD_7_seg bcd_7_seg_3: pin names not known; wires that end beside it: _16_bit_hex_to_bcd_1_d_3, bcd_7_seg_3_p2
  _4_bit_equal_0 _4_bit_equal_0_2 (.I(_16_bit_hex_to_bcd_1_d_3), .O(_4_bit_equal_0_2_o));
  // BCD_7_seg bcd_7_seg_4: pin names not known; wires that end beside it: _16_bit_hex_to_bcd_1_d_4, bcd_7_seg_4_p2
  _4_bit_equal_0 _4_bit_equal_0_3 (.I(_16_bit_hex_to_bcd_1_d_4), .O(_4_bit_equal_0_3_o));
  // BCD_7_seg bcd_7_seg_5: pin names not known; wires that end beside it: _16_bit_hex_to_bcd_1_d_5, bcd_7_seg_5_p2
  _4_bit_equal_0 _4_bit_equal_0_4 (.I(_16_bit_hex_to_bcd_1_d_5), .O(_4_bit_equal_0_4_o));
  and and_1 (and_1_out, _4_bit_equal_0_1_o, and_2_out);
  and and_2 (and_2_out, _4_bit_equal_0_2_o, and_3_out);
  and and_3 (and_3_out, _4_bit_equal_0_3_o, _4_bit_equal_0_4_o);
  // _7_bit_multiplexer _7_bit_multiplexer_1: pin names not known; wires that end beside it: bcd_7_seg_2_p2, {7{1'b0}}, and_1_out, _7_bit_multiplexer_1_p4
  // _7_bit_multiplexer _7_bit_multiplexer_2: pin names not known; wires that end beside it: bcd_7_seg_3_p2, {7{1'b0}}, and_2_out, _7_bit_multiplexer_2_p4
  // _7_bit_multiplexer _7_bit_multiplexer_3: pin names not known; wires that end beside it: bcd_7_seg_4_p2, {7{1'b0}}, and_3_out, _7_bit_multiplexer_3_p4
  // _7_bit_multiplexer _7_bit_multiplexer_4: pin names not known; wires that end beside it: bcd_7_seg_5_p2, {7{1'b0}}, _4_bit_equal_0_4_o, _7_bit_multiplexer_4_p4
  and and_4 (and_4_out, two_compliment_to_singed_number_1_s, and_1_out);
  and and_5 (and_5_out, and_8_out, and_2_out);
  and and_6 (and_6_out, and_9_out, and_3_out);
  and and_7 (and_7_out, and_10_out, _4_bit_equal_0_4_o);
  and and_8 (and_8_out, two_compliment_to_singed_number_1_s, ~and_4_out);  // And
  and and_9 (and_9_out, and_8_out, ~and_5_out);  // And
  and and_10 (and_10_out, and_9_out, ~and_6_out);  // And
  and and_11 (and_11_out, and_10_out, ~and_7_out);  // And
  // _7_bit_multiplexer _7_bit_multiplexer_5: pin names not known; wires that end beside it: _7_bit_multiplexer_1_p4, 7'b1000000, and_4_out, _7_bit_multiplexer_5_p4
  // _7_bit_multiplexer _7_bit_multiplexer_6: pin names not known; wires that end beside it: _7_bit_multiplexer_2_p4, 7'b1000000, and_5_out, _7_bit_multiplexer_6_p4
  // _7_bit_multiplexer _7_bit_multiplexer_7: pin names not known; wires that end beside it: _7_bit_multiplexer_3_p4, 7'b1000000, and_6_out, _7_bit_multiplexer_7_p4
  // _7_bit_multiplexer _7_bit_multiplexer_8: pin names not known; wires that end beside it: _7_bit_multiplexer_4_p4, 7'b1000000, and_7_out, _7_bit_multiplexer_8_p4
  // _7_bit_multiplexer _7_bit_multiplexer_9: pin names not known; wires that end beside it: {7{1'b0}}, 7'b1000000, and_11_out, _7_bit_multiplexer_9_p4
  // _7_seg_to_connector _7_seg_to_connector_1: pin names not known; wires that end beside it: bcd_7_seg_1_o, O[41:35]
  // _7_seg_to_connector _7_seg_to_connector_2: pin names not known; wires that end beside it: _7_bit_multiplexer_5_p4, O[34:28]
  // _7_seg_to_connector _7_seg_to_connector_3: pin names not known; wires that end beside it: _7_bit_multiplexer_6_p4, O[27:21]
  // _7_seg_to_connector _7_seg_to_connector_4: pin names not known; wires that end beside it: _7_bit_multiplexer_7_p4, O[20:14]
  // _7_seg_to_connector _7_seg_to_connector_5: pin names not known; wires that end beside it: _7_bit_multiplexer_8_p4, O[13:7]
  // _7_seg_to_connector _7_seg_to_connector_6: pin names not known; wires that end beside it: _7_bit_multiplexer_9_p4, O[6:0]

  // Notes on the sheet:
  //   takes the first bit,
  //   since its the sign
  //   checks if a four-block of bits is all 0,
  //   cause then for that digit position, the
  //   7-segment-display doesnt need to show anythinght.
  //   checks if this digit is 0, and ands if the ones
  //   before that one were also 0, to see when to put
  //   the minus sign
  //   these multiplexers choose either no lights,
  //   or the BCD of the 4bit number, through a
  //   multiplexer, depending on if they
  //   are four 0s.
  //   hard coded 0000000
  //   These columns of and-gates;
  //   the left one ands if the number is negative and and if the earlier digit position has
  //   no space to show a minus sign. if both are true,
  //   the right column of and-gates checks, if a minus is needed, but not shown yet.
  //   this loops until a minus sign can be shown, if it has to.
  //   hard coded 0000001
  //   this last part transforms each number
  //   in the 7-segment display. each number goes through the
  //   processes explained beforehand.
endmodule
