// Digital circuit 1_bit_multiplexer.dig as structural Verilog
module _1_bit_multiplexer (
  input  A1,
  input  A2,
  input  S,
  output O
);

  wire and_1_out, and_2_out;

  and and_1 (and_1_out, A1, ~S);  // And
  and and_2 (and_2_out, A2, S);
  or or_1 (O, and_1_out, and_2_out);

  // Notes on the sheet:
  //   Input A1 if S is 1, and A2 if S is 0.
endmodule
