// Digital circuit 1_to_12.dig as structural Verilog
module _1_to_12 (
  input  I,
  output [11:0] O
);


  assign O = {12{I}};

  // Notes on the sheet:
  //   one bit turned to 12 of its set state.
endmodule
