// Digital circuit 1_to_4.dig as structural Verilog
module _1_to_4 (
  input  I,
  output [3:0] O
);


  assign O = {4{I}};

  // Notes on the sheet:
  //   1 bit turned into 4 bits of its set state.
endmodule
