// Digital circuit 1_to_8.dig as structural Verilog
module _1_to_8 (
  input  I,
  output [7:0] O
);


  assign O = {8{I}};

  // Notes on the sheet:
  //   Input I gets splitted into 8 bits that are either all set or all not set,
  //   dependant on if I is set or not. Those 8 bits will be Output O.
endmodule
