// Digital circuit 2_bit_decoder.dig as structural Verilog
module _2_bit_decoder (
  input  [1:0] I,
  output [3:0] O
);

  and and_1 (O[0], ~I[0], ~I[1]);  // And
  and and_2 (O[1], I[0], ~I[1]);  // And
  and and_3 (O[2], ~I[0], I[1]);  // And
  and and_4 (O[3], I[0], I[1]);

  // Notes on the sheet:
  //   A decoder which receives Input I, a 2-bit number, and gives out Output O, a 4bit number.
  //   I gets splitted into its 2 bits, and the and-gates check, which bit is set and which isnt.
  //   Lets say the the decimal value of I is n. the 2 to the power of nth bit will be set for O.
endmodule
