// Digital circuit 3_bit_decoder.dig as structural Verilog
module _3_bit_decoder (
  input  [2:0] I,
  output [7:0] O
);

  wire [3:0] _2_bit_decoder_1_o;

  _2_bit_decoder _2_bit_decoder_1 (.I(I[1:0]), .O(_2_bit_decoder_1_o));
  assign O[3:0] = _2_bit_decoder_1_o & ~{4{I[2]}};  // And and_1, 4 bits wide
  assign O[7:4] = _2_bit_decoder_1_o & {4{I[2]}};  // And and_2, 4 bits wide

  // Notes on the sheet:
  //   The Input I has 3 bits, and the Output O has 8 bits. The first two least significant bits get into the 2bit-decoder,
  //   and the most significant bit gets split into four of its type. so if the msb of I is 0, its gets split into 0000, and if
  //   its 1, it gets split into 1111. the split msb now gets anded with the decoder-output twice.
  //   The first four lsbs of O will be determined by the decoder-output anded with the negation of the split msb.
  //   If the msb is 0, it will be negated to 1111, which will "approve" of the decoder-output for the first 4 bits of O,
  //   because it wont be a higher than 4 is the msb of I is 0. if its 1, the decoder-input will be added to the 1, and
  //   the and gates will make sure that it will be the last 4 bits of O.
endmodule
