// Digital circuit 3_bit_decoder_and_lower.dig as structural Verilog
module _3_bit_decoder_and_lower (
  input  [2:0] I,
  output [7:0] _0
);

  wire [6:0] _3_bit_decoder_1_o;

  _3_bit_decoder _3_bit_decoder_1 (.I(I), .O({_0[7], _3_bit_decoder_1_o}));
  or or_1 (_0[6], _3_bit_decoder_1_o[6], _0[7]);
  or or_2 (_0[5], _3_bit_decoder_1_o[5], _0[6]);
  or or_3 (_0[4], _3_bit_decoder_1_o[4], _0[5]);
  or or_4 (_0[3], _3_bit_decoder_1_o[3], _0[4]);
  or or_5 (_0[2], _3_bit_decoder_1_o[2], _0[3]);
  or or_6 (_0[1], _3_bit_decoder_1_o[1], _0[2]);
  or or_7 (_0[0], _3_bit_decoder_1_o[0], _0[1]);

  // Notes on the sheet:
  //   Decodes the 3 bit input into 8 lanes which represent the 6 possible values.
  //   The 3 bit decoder sets the lane that represents the value. 
  //   This module sets that lane all lower lanes.
endmodule
