// Digital circuit 3_bit_multiplexer.dig as structural Verilog
module _3_bit_multiplexer (
  input  [2:0] A1,
  input  [2:0] A2,
  input  S,
  output [2:0] O
);

  _2_bit_multiplexer _2_bit_multiplexer_1 (.A1(A1[1:0]), .A2(A2[1:0]), .S(S), .O(O[1:0]));
  _1_bit_multiplexer _1_bit_multiplexer_1 (.A1(A1[2]), .A2(A2[2]), .S(S), .O(O[2]));

  // Notes on the sheet:
  //   analogous to the 4bit multiplexer, the 3bit multiplexer
  //   works through two connected multiplexers, one 1bit, one 2bit where
  //   the deciding Input S can stay one Input, for its given to
  //   both multiplexers.
endmodule
