// Digital circuit 3_bit_setter.dig as structural Verilog
module _3_bit_setter (
  input  _000,
  input  _001,
  input  _010,
  input  _011,
  input  _100,
  input  _101,
  input  _102,
  input  _111,
  output [2:0] O
);

  wire delay_1_out, or_1_out;
  wire [2:0] _3_bit_multiplexer_1_o, _3_bit_multiplexer_2_o, _3_bit_multiplexer_3_o, _3_bit_multiplexer_4_o,
       _3_bit_multiplexer_5_o, _3_bit_multiplexer_6_o, _3_bit_multiplexer_7_o;

  _3_bit_multiplexer _3_bit_multiplexer_1 (.A1(3'b000), .A2(3'b001), .S(_001), .O(_3_bit_multiplexer_1_o));
  _3_bit_multiplexer _3_bit_multiplexer_2 (
    .A1(_3_bit_multiplexer_1_o), .A2(3'b010), .S(_010), .O(_3_bit_multiplexer_2_o));
  _3_bit_multiplexer _3_bit_multiplexer_3 (
    .A1(_3_bit_multiplexer_2_o), .A2(3'b011), .S(_011), .O(_3_bit_multiplexer_3_o));
  _3_bit_multiplexer _3_bit_multiplexer_4 (
    .A1(_3_bit_multiplexer_3_o), .A2(3'b100), .S(_100), .O(_3_bit_multiplexer_4_o));
  _3_bit_multiplexer _3_bit_multiplexer_5 (
    .A1(_3_bit_multiplexer_4_o), .A2(3'b101), .S(_101), .O(_3_bit_multiplexer_5_o));
  _3_bit_multiplexer _3_bit_multiplexer_6 (
    .A1(_3_bit_multiplexer_5_o), .A2(3'b110), .S(_102), .O(_3_bit_multiplexer_6_o));
  _3_bit_multiplexer _3_bit_multiplexer_7 (
    .A1(_3_bit_multiplexer_6_o), .A2(3'b111), .S(_111), .O(_3_bit_multiplexer_7_o));
  or or_1 (or_1_out, _111, _102, _101, _100, _011, _010, _001, _000);
  D_FF #(.Bits(3)) d_ff_1 (.D(_3_bit_multiplexer_7_o), .C(delay_1_out), .Q(O));  // open: nQ
  Delay #(.delayTime(20)) delay_1 (.in(or_1_out), .out(delay_1_out));

  // Notes on the sheet:
  //   selects the 3 bits chosen based on the operation.
endmodule
