// Digital circuit 4_bit_carry_ripple_adder.dig as structural Verilog
module _4_bit_carry_ripple_adder (
  input  [3:0] A,
  input  [3:0] B,
  input  C_in,
  output [3:0] S,
  output C_out
);

  wire full_adder_1_c_out, full_adder_2_c_out, full_adder_3_c_out;

  full_adder full_adder_1 (.A(A[0]), .B(B[0]), .C_in(C_in), .S(S[0]), .C_out(full_adder_1_c_out));
  full_adder full_adder_2 (.A(A[1]), .B(B[1]), .C_in(full_adder_1_c_out), .S(S[1]), .C_out(full_adder_2_c_out));
  full_adder full_adder_3 (.A(A[2]), .B(B[2]), .C_in(full_adder_2_c_out), .S(S[2]), .C_out(full_adder_3_c_out));
  full_adder full_adder_4 (.A(A[3]), .B(B[3]), .C_in(full_adder_3_c_out), .S(S[3]), .C_out(C_out));

  // Notes on the sheet:
  //   carry select adder with 4 full adder blocks
  //   so that two 4 bit numbers can be added, the inputs
  //   are each split into 1 of the 4 bits and given to each
  //   full-adder
endmodule
