// Digital circuit 4_bit_equal_0.dig as structural Verilog
module _4_bit_equal_0 (
  input  [3:0] I,
  output O
);

  and and_1 (O, ~I[0], ~I[1], ~I[2], ~I[3]);  // And

  // Notes on the sheet:
  //   Is true, if the Input 4bit number I is 0000
endmodule
