// Digital circuit 5_bit_carry_select_adder.dig as structural Verilog
module _5_bit_carry_select_adder (
  input  [4:0] A,
  input  [4:0] B,
  input  C_in,
  output [4:0] S,
  output C_out
);

  wire full_adder_1_c_out, full_adder_1_s, full_adder_2_c_out, full_adder_2_s, full_adder_3_c_out,
       full_adder_3_s, full_adder_4_c_out, full_adder_4_s, full_adder_5_c_out, full_adder_5_s,
       full_adder_6_c_out, full_adder_6_s, full_adder_7_c_out, full_adder_7_s, full_adder_8_c_out,
       full_adder_8_s, full_adder_9_c_out, full_adder_9_s, full_adder_10_c_out, full_adder_10_s;

  full_adder full_adder_1 (.A(A[0]), .B(B[0]), .C_in(1'b0), .S(full_adder_1_s), .C_out(full_adder_1_c_out));
  full_adder full_adder_2 (.A(A[0]), .B(B[0]), .C_in(1'b1), .S(full_adder_2_s), .C_out(full_adder_2_c_out));
  _1_bit_multiplexer _1_bit_multiplexer_1 (.A1(full_adder_1_s), .A2(full_adder_2_s), .S(C_in), .O(S[0]));
  full_adder full_adder_3 (
    .A(A[1]), .B(B[1]), .C_in(full_adder_1_c_out), .S(full_adder_3_s), .C_out(full_adder_3_c_out));
  full_adder full_adder_4 (
    .A(A[1]), .B(B[1]), .C_in(full_adder_2_c_out), .S(full_adder_4_s), .C_out(full_adder_4_c_out));
  full_adder full_adder_5 (
    .A(A[2]), .B(B[2]), .C_in(full_adder_3_c_out), .S(full_adder_5_s), .C_out(full_adder_5_c_out));
  full_adder full_adder_6 (
    .A(A[2]), .B(B[2]), .C_in(full_adder_4_c_out), .S(full_adder_6_s), .C_out(full_adder_6_c_out));
  _1_bit_multiplexer _1_bit_multiplexer_2 (.A1(full_adder_3_s), .A2(full_adder_4_s), .S(C_in), .O(S[1]));
  _1_bit_multiplexer _1_bit_multiplexer_3 (.A1(full_adder_5_s), .A2(full_adder_6_s), .S(C_in), .O(S[2]));
  full_adder full_adder_7 (
    .A(A[3]), .B(B[3]), .C_in(full_adder_5_c_out), .S(full_adder_7_s), .C_out(full_adder_7_c_out));
  full_adder full_adder_8 (
    .A(A[3]), .B(B[3]), .C_in(full_adder_6_c_out), .S(full_adder_8_s), .C_out(full_adder_8_c_out));
  _1_bit_multiplexer _1_bit_multiplexer_4 (.A1(full_adder_7_s), .A2(full_adder_8_s), .S(C_in), .O(S[3]));
  full_adder full_adder_9 (
    .A(A[4]), .B(B[4]), .C_in(full_adder_7_c_out), .S(full_adder_9_s), .C_out(full_adder_9_c_out));
  full_adder full_adder_10 (
    .A(A[4]), .B(B[4]), .C_in(full_adder_8_c_out), .S(full_adder_10_s), .C_out(full_adder_10_c_out));
  _1_bit_multiplexer _1_bit_multiplexer_5 (.A1(full_adder_9_s), .A2(full_adder_10_s), .S(C_in), .O(S[4]));
  _1_bit_multiplexer _1_bit_multiplexer_6 (.A1(full_adder_9_c_out), .A2(full_adder_10_c_out), .S(C_in), .O(C_out));

  // Notes on the sheet:
  //   5bit carry select adder that calculates the carry out for the next one,
  //   if the carry in from the previous is 0 and 1, and at the end selects the
  //   correct computation.
endmodule
