// Digital circuit 7_bit_multiplexer.dig as structural Verilog
module _7_bit_multiplexer (
  input  [6:0] A1,
  input  [6:0] A2,
  input  S,
  output [6:0] O
);

  _4_bit_multiplexer _4_bit_multiplexer_1 (.A1(A1[3:0]), .A2(A2[3:0]), .S(S), .O(O[3:0]));
  _3_bit_multiplexer _3_bit_multiplexer_1 (.A1(A1[6:4]), .A2(A2[6:4]), .S(S), .O(O[6:4]));

  // Notes on the sheet:
  //   analogous to the 8bit multiplexer, the 7bit multiplexer
  //   works through a 3 and a 4bit multiplexer, where
  //   the deciding Input S can stay one Input, for its given to
  //   both bit multiplexers, and the outputs will be concatenated
  //   to a 7bit output.
endmodule
