// Digital circuit 7_seg_to_connector.dig as structural Verilog
module _7_seg_to_connector (
  input  [6:0] I,
  output [6:0] O
);

  // Pins of 1 and 7 bits meet at I
  // Pins of 1 and 7 bits meet at {I[6:4], I[0], I[1], I[2], I[3]}

  assign O = {I[6:4], I[0], I[1], I[2], I[3]};

  // Notes on the sheet:
  //   Each 7-segment-lights have names from A-G, we switched those up a bit 
  //   so the displays fit neater.
endmodule
