// Digital circuit 8_bit_3_bit_multiplexer.dig as structural Verilog
module _8_bit_3_bit_multiplexer (
  input  [2:0] S,
  input  [7:0] A1,
  input  [7:0] A2,
  input  [7:0] A3,
  input  [7:0] A4,
  input  [7:0] A5,
  input  [7:0] A6,
  input  [7:0] A7,
  input  [7:0] A8,
  output [7:0] O
);

  wire [7:0] _3_bit_decoder_1_o, _8_bit_multiplexer_1_o, _8_bit_multiplexer_2_o, _8_bit_multiplexer_3_o,
       _8_bit_multiplexer_4_o, _8_bit_multiplexer_5_o, _8_bit_multiplexer_6_o;

  _3_bit_decoder _3_bit_decoder_1 (.I(S), .O(_3_bit_decoder_1_o));
  _8_bit_multiplexer _8_bit_multiplexer_1 (.A1(A1), .A2(A2), .S(_3_bit_decoder_1_o[1]), .O(_8_bit_multiplexer_1_o));
  _8_bit_multiplexer _8_bit_multiplexer_2 (
    .A1(_8_bit_multiplexer_1_o), .A2(A3), .S(_3_bit_decoder_1_o[2]), .O(_8_bit_multiplexer_2_o));
  _8_bit_multiplexer _8_bit_multiplexer_3 (
    .A1(_8_bit_multiplexer_2_o), .A2(A4), .S(_3_bit_decoder_1_o[3]), .O(_8_bit_multiplexer_3_o));
  _8_bit_multiplexer _8_bit_multiplexer_4 (
    .A1(_8_bit_multiplexer_3_o), .A2(A5), .S(_3_bit_decoder_1_o[4]), .O(_8_bit_multiplexer_4_o));
  _8_bit_multiplexer _8_bit_multiplexer_5 (
    .A1(_8_bit_multiplexer_4_o), .A2(A6), .S(_3_bit_decoder_1_o[5]), .O(_8_bit_multiplexer_5_o));
  _8_bit_multiplexer _8_bit_multiplexer_6 (
    .A1(_8_bit_multiplexer_5_o), .A2(A7), .S(_3_bit_decoder_1_o[6]), .O(_8_bit_multiplexer_6_o));
  _8_bit_multiplexer _8_bit_multiplexer_7 (.A1(_8_bit_multiplexer_6_o), .A2(A8), .S(_3_bit_decoder_1_o[7]), .O(O));

  // Notes on the sheet:
  //   One of the Inputs is chosen based on Input S, as its
  //   3 bits get decoded, and then the 2^nth one will decide
  //   on the operation.
endmodule
