// Digital circuit 8_bit_4_value_setter.dig as structural Verilog
module _8_bit_4_value_setter (
  input  [7:0] I_1,
  input  S_1,
  input  [7:0] I_2,
  input  S_2,
  input  [7:0] I_3,
  input  S_3,
  input  [7:0] I_4,
  input  S_4,
  output [7:0] O
);

  wire delay_1_out, or_1_out;
  wire [7:0] _8_bit_multiplexer_1_o, _8_bit_multiplexer_2_o, _8_bit_multiplexer_3_o, _8_bit_multiplexer_4_o;

  _8_bit_multiplexer _8_bit_multiplexer_1 (.A1({8{1'b0}}), .A2(I_1), .S(S_1), .O(_8_bit_multiplexer_1_o));
  _8_bit_multiplexer _8_bit_multiplexer_2 (.A1(_8_bit_multiplexer_1_o), .A2(I_2), .S(S_2), .O(_8_bit_multiplexer_2_o));
  _8_bit_multiplexer _8_bit_multiplexer_3 (.A1(_8_bit_multiplexer_2_o), .A2(I_3), .S(S_3), .O(_8_bit_multiplexer_3_o));
  _8_bit_multiplexer _8_bit_multiplexer_4 (.A1(_8_bit_multiplexer_3_o), .A2(I_4), .S(S_4), .O(_8_bit_multiplexer_4_o));
  or or_1 (or_1_out, S_4, S_3, S_2, S_1);
  D_FF #(.Bits(8)) d_ff_1 (.D(_8_bit_multiplexer_4_o), .C(delay_1_out), .Q(O));  // open: nQ
  Delay #(.delayTime(10)) delay_1 (.in(or_1_out), .out(delay_1_out));

  // Notes on the sheet:
  //   multiplexes a constant zero with first input I depending on deciding Input S_,
  //   so the adder adds nothing to I_1, which gets then Multiplexed with the next I
  //   based on the next S. All the S Inputs will be ored and after a delay flip flopped.
endmodule
