// Digital circuit 8_bit_adder.dig as structural Verilog
module _8_bit_adder (
  input  [7:0] A,
  input  [7:0] B,
  output [7:0] S
);

  wire _3_bit_carry_ripple_adder_1_c_out;

  _3_bit_carry_ripple_adder _3_bit_carry_ripple_adder_1 (
    .A(A[2:0]), .B(B[2:0]), .C_in(1'b0), .S(S[2:0]), .C_out(_3_bit_carry_ripple_adder_1_c_out));
  _5_bit_carry_select_adder _5_bit_carry_select_adder_1 (
    .A(A[7:3]), .B(B[7:3]), .C_in(_3_bit_carry_ripple_adder_1_c_out), .S(S[7:3]));  // open: C_out

  // Notes on the sheet:
  //   Input A and B get their first 3 through a ripple carry adder
  //   and the last 5 bits through a carry select adder, and the sum of both
  //   Inputs is S.
endmodule
