// Digital circuit 8_bit_alu.dig as structural Verilog
module _8_bit_alu (
  input  [7:0] A,
  input  [7:0] B,
  input  [2:0] O,
  output [7:0] Y
);

  wire and_1_out;
  wire [7:0] _1_to_8_1_o, _8_bit_adder_1_s, _8_bit_adder_2_s, _8_bit_adder_3_s, and_2_out,
       shift_8_bit_by_8_1_y, shift_8_bit_by_8_2_y, shift_8_bit_by_8_3_y, shift_8_bit_by_8_4_y;
  wire [27:0] _8_bit_to_4_7_sec_connector_1_o;

  shift_8_bit_by_8 shift_8_bit_by_8_1 (.A(A), .B(B), .O(1'b0), .Y(shift_8_bit_by_8_1_y));
  shift_8_bit_by_8 shift_8_bit_by_8_2 (.A(A), .B(B), .O(1'b1), .Y(shift_8_bit_by_8_2_y));
  shift_8_bit_by_8 shift_8_bit_by_8_3 (.A(A), .B(8'h1), .O(1'b0), .Y(shift_8_bit_by_8_3_y));
  shift_8_bit_by_8 shift_8_bit_by_8_4 (.A(B), .B(8'h4), .O(1'b0), .Y(shift_8_bit_by_8_4_y));
  _8_bit_adder _8_bit_adder_1 (.A(A), .B(B), .S(_8_bit_adder_1_s));
  _8_bit_adder _8_bit_adder_2 (.A(A), .B(8'h1), .S(_8_bit_adder_2_s));
  _8_bit_adder _8_bit_adder_3 (.A(A), .B({8{1'b1}}), .S(_8_bit_adder_3_s));
  _8_bit_3_bit_multiplexer _8_bit_3_bit_multiplexer_1 (
    .S(O), .A1(shift_8_bit_by_8_1_y), .A2(shift_8_bit_by_8_2_y), .A3(shift_8_bit_by_8_3_y),
    .A4(shift_8_bit_by_8_4_y), .A5(_8_bit_adder_1_s), .A6(_8_bit_adder_2_s), .A7(_8_bit_adder_3_s),
    .A8(8'hd), .O(Y));
  _8_bit_to_4_7_sec_connector _8_bit_to_4_7_sec_connector_1 (.I(and_2_out), .O(_8_bit_to_4_7_sec_connector_1_o));
  and and_1 (and_1_out, O[0], O[1], ~O[2]);  // And
  Seven_Seg seven_seg_1 (
    .a(_8_bit_to_4_7_sec_connector_1_o[3]), .b(_8_bit_to_4_7_sec_connector_1_o[2]),
    .c(_8_bit_to_4_7_sec_connector_1_o[1]), .d(_8_bit_to_4_7_sec_connector_1_o[0]),
    .e(_8_bit_to_4_7_sec_connector_1_o[4]), .f(_8_bit_to_4_7_sec_connector_1_o[5]),
    .g(_8_bit_to_4_7_sec_connector_1_o[6]), .dp(1'b0));
  _1_to_8 _1_to_8_1 (.I(and_1_out), .O(_1_to_8_1_o));
  assign and_2_out = _1_to_8_1_o & A;  // And and_2, 8 bits wide
  Seven_Seg seven_seg_2 (
    .a(_8_bit_to_4_7_sec_connector_1_o[10]), .b(_8_bit_to_4_7_sec_connector_1_o[9]),
    .c(_8_bit_to_4_7_sec_connector_1_o[8]), .d(_8_bit_to_4_7_sec_connector_1_o[7]),
    .e(_8_bit_to_4_7_sec_connector_1_o[11]), .f(_8_bit_to_4_7_sec_connector_1_o[12]),
    .g(_8_bit_to_4_7_sec_connector_1_o[13]), .dp(1'b0));
  Seven_Seg seven_seg_3 (
    .a(_8_bit_to_4_7_sec_connector_1_o[17]), .b(_8_bit_to_4_7_sec_connector_1_o[16]),
    .c(_8_bit_to_4_7_sec_connector_1_o[15]), .d(_8_bit_to_4_7_sec_connector_1_o[14]),
    .e(_8_bit_to_4_7_sec_connector_1_o[18]), .f(_8_bit_to_4_7_sec_connector_1_o[19]),
    .g(_8_bit_to_4_7_sec_connector_1_o[20]), .dp(1'b0));
  Seven_Seg seven_seg_4 (
    .a(_8_bit_to_4_7_sec_connector_1_o[24]), .b(_8_bit_to_4_7_sec_connector_1_o[23]),
    .c(_8_bit_to_4_7_sec_connector_1_o[22]), .d(_8_bit_to_4_7_sec_connector_1_o[21]),
    .e(_8_bit_to_4_7_sec_connector_1_o[25]), .f(_8_bit_to_4_7_sec_connector_1_o[26]),
    .g(_8_bit_to_4_7_sec_connector_1_o[27]), .dp(1'b0));

  // Notes on the sheet:
  //   A << B
  //   A >> B
  //   A << 1
  //   _*
  //   A + B
  //   A + 1
  //   A - 1
  //   13_10
  //   each operations are being calculated, before a multiplexer chooses the
  //   one which was the one asked for.
endmodule
