// Digital circuit 8_bit_multiplexer.dig as structural Verilog
module _8_bit_multiplexer (
  input  [7:0] A1,
  input  [7:0] A2,
  input  S,
  output [7:0] O
);

  _4_bit_multiplexer _4_bit_multiplexer_1 (.A1(A1[3:0]), .A2(A2[3:0]), .S(S), .O(O[3:0]));
  _4_bit_multiplexer _4_bit_multiplexer_2 (.A1(A1[7:4]), .A2(A2[7:4]), .S(S), .O(O[7:4]));

  // Notes on the sheet:
  //   analogous to the 16bit multiplexer, the 8bit multiplexer
  //   works through two connected 4bit multiplexers, where
  //   the deciding Input S can stay one Input, for its given to
  //   both 1bit multiplexers.
endmodule
