// Digital circuit 8_bit_to_4_7_sec_connector.dig as structural Verilog
module _8_bit_to_4_7_sec_connector (
  input  [7:0] I,
  output [27:0] O
);

  wire _4_bit_equal_0_1_o, _4_bit_equal_0_2_o, _7_bit_multiplexer_1_p4, _7_bit_multiplexer_2_p4,
       _7_bit_multiplexer_3_p4, _7_bit_multiplexer_4_p4, _7_bit_multiplexer_5_p4,
       _8_bit_two_compliment_to_singed_number_1_s, and_1_out, and_2_out, and_3_out, and_4_out, and_5_out,
       bcd_7_seg_1_o, bcd_7_seg_2_p2, bcd_7_seg_3_p2;
  wire [3:0] _8_bit_to_bcd_1_d_1, _8_bit_to_bcd_1_d_2, _8_bit_to_bcd_1_d_3;
  wire [7:0] _8_bit_two_compliment_to_singed_number_1_o;

  _8_bit_two_compliment_to_singed_number _8_bit_two_compliment_to_singed_number_1 (
    .I(I), .O(_8_bit_two_compliment_to_singed_number_1_o), .S(_8_bit_two_compliment_to_singed_number_1_s));
  _8_bit_to_BCD _8_bit_to_bcd_1 (
    .I(_8_bit_two_compliment_to_singed_number_1_o), .D_1(_8_bit_to_bcd_1_d_1), .D_2(_8_bit_to_bcd_1_d_2),
    .D_3(_8_bit_to_bcd_1_d_3));
  BCD_7_seg bcd_7_seg_1 (.I(_8_bit_to_bcd_1_d_1), .O(bcd_7_seg_1_o));
  // BCD_7_seg bcd_7_seg_2: pin names not known; wires that end beside it: _8_bit_to_bcd_1_d_2, bcd_7_seg_2_p2
  _4_bit_equal_0 _4_bit_equal_0_1 (.I(_8_bit_to_bcd_1_d_2), .O(_4_bit_equal_0_1_o));
  // BCD_7_seg bcd_7_seg_3: pin names not known; wires that end beside it: _8_bit_to_bcd_1_d_3, bcd_7_seg_3_p2
  _4_bit_equal_0 _4_bit_equal_0_2 (.I(_8_bit_to_bcd_1_d_3), .O(_4_bit_equal_0_2_o));
  and and_1 (and_1_out, _4_bit_equal_0_1_o, _4_bit_equal_0_2_o);
  // _7_bit_multiplexer _7_bit_multiplexer_1: pin names not known; wires that end beside it: bcd_7_seg_2_p2, {7{1'b0}}, and_1_out, _7_bit_multiplexer_1_p4
  // _7_bit_multiplexer _7_bit_multiplexer_2: pin names not known; wires that end beside it: bcd_7_seg_3_p2, {7{1'b0}}, _4_bit_equal_0_2_o, _7_bit_multiplexer_2_p4
  and and_2 (and_2_out, _8_bit_two_compliment_to_singed_number_1_s, and_1_out);
  and and_3 (and_3_out, and_4_out, _4_bit_equal_0_2_o);
  and and_4 (and_4_out, _8_bit_two_compliment_to_singed_number_1_s, ~and_2_out);  // And
  and and_5 (and_5_out, and_4_out, ~and_3_out);  // And
  // _7_bit_multiplexer _7_bit_multiplexer_3: pin names not known; wires that end beside it: _7_bit_multiplexer_1_p4, 7'b1000000, and_2_out, _7_bit_multiplexer_3_p4
  // _7_bit_multiplexer _7_bit_multiplexer_4: pin names not known; wires that end beside it: _7_bit_multiplexer_2_p4, 7'b1000000, and_3_out, _7_bit_multiplexer_4_p4
  // _7_bit_multiplexer _7_bit_multiplexer_5: pin names not known; wires that end beside it: {7{1'b0}}, 7'b1000000, and_5_out, _7_bit_multiplexer_5_p4
  // _7_seg_to_connector _7_seg_to_connector_1: pin names not known; wires that end beside it: bcd_7_seg_1_o, O[27:21]
  // _7_seg_to_connector _7_seg_to_connector_2: pin names not known; wires that end beside it: _7_bit_multiplexer_3_p4, O[20:14]
  // _7_seg_to_connector _7_seg_to_connector_3: pin names not known; wires that end beside it: _7_bit_multiplexer_4_p4, O[13:7]
  // _7_seg_to_connector _7_seg_to_connector_4: pin names not known; wires that end beside it: _7_bit_multiplexer_5_p4, O[6:0]

  // Notes on the sheet:
  //   8 bits get turned into 4 to display digit positions for the 7-segment-display.
  //   everything is analogous to exercise 3.
endmodule
