// Digital circuit 8_bit_to_BCD.dig as structural Verilog
module _8_bit_to_BCD (
  input  [7:0] I,
  output [3:0] D_1,
  output [3:0] D_2,
  output [3:0] D_3
);

  wire to_bcd_block_1_o_1, to_bcd_block_1_o_2, to_bcd_block_1_o_3, to_bcd_block_1_o_4, to_bcd_block_2_o_1,
       to_bcd_block_2_o_2, to_bcd_block_2_o_3, to_bcd_block_2_o_4, to_bcd_block_3_o_1, to_bcd_block_3_o_2,
       to_bcd_block_3_o_3, to_bcd_block_3_o_4, to_bcd_block_4_o_1, to_bcd_block_4_o_2, to_bcd_block_4_o_3,
       to_bcd_block_4_o_4, to_bcd_block_5_o_1, to_bcd_block_5_o_2, to_bcd_block_5_o_3;

  to_BCD_block to_bcd_block_1 (
    .x_1(I[5]), .x_2(I[6]), .x_3(I[7]), .x_4(1'b0), .o_1(to_bcd_block_1_o_1), .o_2(to_bcd_block_1_o_2),
    .o_3(to_bcd_block_1_o_3), .o_4(to_bcd_block_1_o_4));
  to_BCD_block to_bcd_block_2 (
    .x_1(I[4]), .x_2(to_bcd_block_1_o_1), .x_3(to_bcd_block_1_o_2), .x_4(to_bcd_block_1_o_3),
    .o_1(to_bcd_block_2_o_1), .o_2(to_bcd_block_2_o_2), .o_3(to_bcd_block_2_o_3), .o_4(to_bcd_block_2_o_4));
  to_BCD_block to_bcd_block_3 (
    .x_1(I[3]), .x_2(to_bcd_block_2_o_1), .x_3(to_bcd_block_2_o_2), .x_4(to_bcd_block_2_o_3),
    .o_1(to_bcd_block_3_o_1), .o_2(to_bcd_block_3_o_2), .o_3(to_bcd_block_3_o_3), .o_4(to_bcd_block_3_o_4));
  to_BCD_block to_bcd_block_4 (
    .x_1(I[2]), .x_2(to_bcd_block_3_o_1), .x_3(to_bcd_block_3_o_2), .x_4(to_bcd_block_3_o_3),
    .o_1(to_bcd_block_4_o_1), .o_2(to_bcd_block_4_o_2), .o_3(to_bcd_block_4_o_3), .o_4(to_bcd_block_4_o_4));
  to_BCD_block to_bcd_block_5 (
    .x_1(to_bcd_block_3_o_4), .x_2(to_bcd_block_2_o_4), .x_3(to_bcd_block_1_o_4), .x_4(1'b0),
    .o_1(to_bcd_block_5_o_1), .o_2(to_bcd_block_5_o_2), .o_3(to_bcd_block_5_o_3), .o_4(D_3[1]));
  to_BCD_block to_bcd_block_6 (
    .x_1(I[1]), .x_2(to_bcd_block_4_o_1), .x_3(to_bcd_block_4_o_2), .x_4(to_bcd_block_4_o_3), .o_1(D_1[1]),
    .o_2(D_1[2]), .o_3(D_1[3]), .o_4(D_2[0]));
  to_BCD_block to_bcd_block_7 (
    .x_1(to_bcd_block_4_o_4), .x_2(to_bcd_block_5_o_1), .x_3(to_bcd_block_5_o_2), .x_4(to_bcd_block_5_o_3),
    .o_1(D_2[1]), .o_2(D_2[2]), .o_3(D_2[3]), .o_4(D_3[0]));

  assign D_1[0] = I[0];
  assign D_3[3:2] = 2'b00;

  // Notes on the sheet:
  //   analogous to the one with 5 output digit positions from exercise 3.
endmodule
