// Digital circuit 8_bit_two_compliment_to_singed_number.dig as structural Verilog
module _8_bit_two_compliment_to_singed_number (
  input  [7:0] I,
  output [7:0] O,
  output S
);

  wire [7:0] _8_bit_adder_1_s, not_1_out;

  assign not_1_out = ~I;  // Not not_1, 8 bits wide
  _8_bit_adder _8_bit_adder_1 (.A(not_1_out), .B(8'h1), .S(_8_bit_adder_1_s));
  _8_bit_multiplexer _8_bit_multiplexer_1 (.A1(I), .A2(_8_bit_adder_1_s), .S(I[7]), .O(O));

  assign S = I[7];

  // Notes on the sheet:
  //   analogous to exercise 3.
endmodule
