// Digital circuit BCD_7_seg.dig as structural Verilog
module BCD_7_seg (
  input  [3:0] I,
  output [6:0] O
);

  wire and_1_out, and_2_out, and_3_out, and_4_out, and_5_out, and_6_out, and_7_out, and_8_out, and_9_out;

  and and_1 (and_1_out, ~I[2], ~I[0]);  // And
  and and_2 (and_2_out, I[2], I[0]);
  and and_3 (and_3_out, ~I[1], ~I[0]);  // And
  and and_4 (and_4_out, I[1], I[0]);
  and and_5 (and_5_out, ~I[2], I[1]);  // And
  and and_6 (and_6_out, I[2], ~I[1], I[0]);  // And
  and and_7 (and_7_out, I[1], ~I[0]);  // And
  and and_8 (and_8_out, I[2], ~I[1]);  // And
  and and_9 (and_9_out, I[2], ~I[0]);  // And
  or or_1 (O[0], I[3], I[1], and_1_out, and_2_out);
  or or_2 (O[1], ~I[2], and_3_out, and_4_out);  // Or
  or or_3 (O[2], I[2], ~I[1], I[0]);  // Or
  or or_4 (O[3], I[3], and_5_out, and_6_out, and_1_out, and_7_out);
  or or_5 (O[4], and_7_out, and_1_out);
  or or_6 (O[5], I[3], and_8_out, and_9_out, and_3_out);
  or or_7 (O[6], I[3], and_5_out, and_8_out, and_9_out);
  // Pins of 1 and 7 bits meet at O

  // Notes on the sheet:
  //   From: https://www.geeksforgeeks.org/bcd-to-7-segment-decoder/
  //   1, 2, 3
  //   (!1 & !3)
  //   (1 & 3)
  //   (!2 & !3)
  //   (2 & 3)
  //   (!1 & 2)
  //   (1 & !2 & 3)
  //   (2 & !3)
  //   (1 & !2)
  //   (1 & !3)
  //   0, 1, 2, 3
  //   The logic behind which specific 7-segment-display
  //   lights are turned on and off for each number.
  //   A = 0 | 2 | (!1 & !3) | (1 & 3)
  //   B = !1 | (!2 & !3) | (2 & 3)
  //   C = 1 | !2 | 3
  //   D = 0 | (!1 & 2)  | (1 & !2 & 3) |  (!1 & !3)  | (2 & !3)
  //   E =  (2 & !3) | (!1 & !3)
  //   F = 0 | (1 & !2) | (1 & !3) |  (!2 & !3)
  //   G = 0 | (!1 & 2) | (1 & !2)  | (1 & !3)
endmodule
