// Digital circuit __Exercise_1_tester.dig as structural Verilog
module Exercise_1_tester (
  input  [7:0] A,
  input  [7:0] B,
  input  O
);

  wire [7:0] shift_8_bit_by_8_1_y;

  shift_8_bit_by_8 shift_8_bit_by_8_1 (.A(A), .B(B), .O(O), .Y(shift_8_bit_by_8_1_y));

  // Notes on the sheet:
  //   Use this to test! :)
endmodule
