// Digital circuit __Exercise_2_tester.dig as structural Verilog
module Exercise_2_tester (
  input  [7:0] A,
  input  [7:0] B
);

  wire [3:0] _8_bit_adder_1_s, _8_bit_adder_1_s_2;

  _8_bit_adder _8_bit_adder_1 (.A(A), .B(B), .S({_8_bit_adder_1_s_2, _8_bit_adder_1_s}));
  Seven_Seg_Hex seven_seg_hex_1 (.d(_8_bit_adder_1_s_2), .dp(1'b0));
  Seven_Seg_Hex seven_seg_hex_2 (.d(_8_bit_adder_1_s), .dp(1'b0));

  // Notes on the sheet:
  //   tester for the 8bit adder
endmodule
