// Digital circuit __Exercise_4_tester.dig as structural Verilog
module Exercise_4_tester (
);

  wire button_1_out, button_2_out, button_3_out, button_4_out, button_5_out, button_6_out, button_7_out,
       button_8_out, button_9_out, button_10_out, button_11_out, button_12_out, button_13_out, button_14_out,
       button_15_out, button_16_out;
  wire [2:0] _3_bit_setter_1_o;
  wire [7:0] _8_bit_4_value_setter_1_o, _8_bit_4_value_setter_2_o, _8_bit_alu_1_y;
  wire [27:0] _8_bit_to_4_7_sec_connector_1_o, _8_bit_to_4_7_sec_connector_2_o,
       _8_bit_to_4_7_sec_connector_3_o;

  Button button_1 (.out(button_1_out));
  Button button_2 (.out(button_2_out));
  Button button_3 (.out(button_3_out));
  Button button_4 (.out(button_4_out));
  Button button_5 (.out(button_5_out));
  Button button_6 (.out(button_6_out));
  Button button_7 (.out(button_7_out));
  Button button_8 (.out(button_8_out));
  Button button_9 (.out(button_9_out));
  Button button_10 (.out(button_10_out));
  Button button_11 (.out(button_11_out));
  Button button_12 (.out(button_12_out));
  Button button_13 (.out(button_13_out));
  Button button_14 (.out(button_14_out));
  Button button_15 (.out(button_15_out));
  Button button_16 (.out(button_16_out));
  _8_bit_4_value_setter _8_bit_4_value_setter_1 (
    .I_1({8{1'b0}}), .S_1(button_1_out), .I_2(8'h5), .S_2(button_2_out), .I_3(8'hfb), .S_3(button_3_out),
    .I_4(8'h21), .S_4(button_4_out), .O(_8_bit_4_value_setter_1_o));
  _3_bit_setter _3_bit_setter_1 (
    ._000(button_5_out), ._001(button_6_out), ._010(button_7_out), ._011(button_8_out), ._100(button_9_out),
    ._101(button_10_out), ._102(button_11_out), ._111(button_12_out), .O(_3_bit_setter_1_o));
  _8_bit_4_value_setter _8_bit_4_value_setter_2 (
    .I_1({8{1'b0}}), .S_1(button_13_out), .I_2(8'h5), .S_2(button_14_out), .I_3(8'hfb), .S_3(button_15_out),
    .I_4(8'h21), .S_4(button_16_out), .O(_8_bit_4_value_setter_2_o));
  _8_bit_alu _8_bit_alu_1 (
    .A(_8_bit_4_value_setter_1_o), .B(_8_bit_4_value_setter_2_o), .O(_3_bit_setter_1_o), .Y(_8_bit_alu_1_y));
  _8_bit_to_4_7_sec_connector _8_bit_to_4_7_sec_connector_1 (
    .I(_8_bit_4_value_setter_1_o), .O(_8_bit_to_4_7_sec_connector_1_o));
  _8_bit_to_4_7_sec_connector _8_bit_to_4_7_sec_connector_2 (
    .I(_8_bit_4_value_setter_2_o), .O(_8_bit_to_4_7_sec_connector_2_o));
  _8_bit_to_4_7_sec_connector _8_bit_to_4_7_sec_connector_3 (.I(_8_bit_alu_1_y), .O(_8_bit_to_4_7_sec_connector_3_o));
  Seven_Seg seven_seg_1 (
    .a(_8_bit_to_4_7_sec_connector_1_o[3]), .b(_8_bit_to_4_7_sec_connector_1_o[2]),
    .c(_8_bit_to_4_7_sec_connector_1_o[1]), .d(_8_bit_to_4_7_sec_connector_1_o[0]),
    .e(_8_bit_to_4_7_sec_connector_1_o[4]), .f(_8_bit_to_4_7_sec_connector_1_o[5]),
    .g(_8_bit_to_4_7_sec_connector_1_o[6]), .dp(1'b0));
  Seven_Seg seven_seg_2 (
    .a(_8_bit_to_4_7_sec_connector_2_o[3]), .b(_8_bit_to_4_7_sec_connector_2_o[2]),
    .c(_8_bit_to_4_7_sec_connector_2_o[1]), .d(_8_bit_to_4_7_sec_connector_2_o[0]),
    .e(_8_bit_to_4_7_sec_connector_2_o[4]), .f(_8_bit_to_4_7_sec_connector_2_o[5]),
    .g(_8_bit_to_4_7_sec_connector_2_o[6]), .dp(1'b0));
  Seven_Seg seven_seg_3 (
    .a(_8_bit_to_4_7_sec_connector_3_o[3]), .b(_8_bit_to_4_7_sec_connector_3_o[2]),
    .c(_8_bit_to_4_7_sec_connector_3_o[1]), .d(_8_bit_to_4_7_sec_connector_3_o[0]),
    .e(_8_bit_to_4_7_sec_connector_3_o[4]), .f(_8_bit_to_4_7_sec_connector_3_o[5]),
    .g(_8_bit_to_4_7_sec_connector_3_o[6]), .dp(1'b0));
  Seven_Seg seven_seg_4 (
    .a(_8_bit_to_4_7_sec_connector_1_o[10]), .b(_8_bit_to_4_7_sec_connector_1_o[9]),
    .c(_8_bit_to_4_7_sec_connector_1_o[8]), .d(_8_bit_to_4_7_sec_connector_1_o[7]),
    .e(_8_bit_to_4_7_sec_connector_1_o[11]), .f(_8_bit_to_4_7_sec_connector_1_o[12]),
    .g(_8_bit_to_4_7_sec_connector_1_o[13]), .dp(1'b0));
  Seven_Seg seven_seg_5 (
    .a(_8_bit_to_4_7_sec_connector_2_o[10]), .b(_8_bit_to_4_7_sec_connector_2_o[9]),
    .c(_8_bit_to_4_7_sec_connector_2_o[8]), .d(_8_bit_to_4_7_sec_connector_2_o[7]),
    .e(_8_bit_to_4_7_sec_connector_2_o[11]), .f(_8_bit_to_4_7_sec_connector_2_o[12]),
    .g(_8_bit_to_4_7_sec_connector_2_o[13]), .dp(1'b0));
  Seven_Seg seven_seg_6 (
    .a(_8_bit_to_4_7_sec_connector_3_o[10]), .b(_8_bit_to_4_7_sec_connector_3_o[9]),
    .c(_8_bit_to_4_7_sec_connector_3_o[8]), .d(_8_bit_to_4_7_sec_connector_3_o[7]),
    .e(_8_bit_to_4_7_sec_connector_3_o[11]), .f(_8_bit_to_4_7_sec_connector_3_o[12]),
    .g(_8_bit_to_4_7_sec_connector_3_o[13]), .dp(1'b0));
  Seven_Seg seven_seg_7 (
    .a(_8_bit_to_4_7_sec_connector_1_o[17]), .b(_8_bit_to_4_7_sec_connector_1_o[16]),
    .c(_8_bit_to_4_7_sec_connector_1_o[15]), .d(_8_bit_to_4_7_sec_connector_1_o[14]),
    .e(_8_bit_to_4_7_sec_connector_1_o[18]), .f(_8_bit_to_4_7_sec_connector_1_o[19]),
    .g(_8_bit_to_4_7_sec_connector_1_o[20]), .dp(1'b0));
  Seven_Seg seven_seg_8 (
    .a(_8_bit_to_4_7_sec_connector_2_o[17]), .b(_8_bit_to_4_7_sec_connector_2_o[16]),
    .c(_8_bit_to_4_7_sec_connector_2_o[15]), .d(_8_bit_to_4_7_sec_connector_2_o[14]),
    .e(_8_bit_to_4_7_sec_connector_2_o[18]), .f(_8_bit_to_4_7_sec_connector_2_o[19]),
    .g(_8_bit_to_4_7_sec_connector_2_o[20]), .dp(1'b0));
  Seven_Seg seven_seg_9 (
    .a(_8_bit_to_4_7_sec_connector_3_o[17]), .b(_8_bit_to_4_7_sec_connector_3_o[16]),
    .c(_8_bit_to_4_7_sec_connector_3_o[15]), .d(_8_bit_to_4_7_sec_connector_3_o[14]),
    .e(_8_bit_to_4_7_sec_connector_3_o[18]), .f(_8_bit_to_4_7_sec_connector_3_o[19]),
    .g(_8_bit_to_4_7_sec_connector_3_o[20]), .dp(1'b0));
  Seven_Seg seven_seg_10 (
    .a(_8_bit_to_4_7_sec_connector_1_o[24]), .b(_8_bit_to_4_7_sec_connector_1_o[23]),
    .c(_8_bit_to_4_7_sec_connector_1_o[22]), .d(_8_bit_to_4_7_sec_connector_1_o[21]),
    .e(_8_bit_to_4_7_sec_connector_1_o[25]), .f(_8_bit_to_4_7_sec_connector_1_o[26]),
    .g(_8_bit_to_4_7_sec_connector_1_o[27]), .dp(1'b0));
  Seven_Seg seven_seg_11 (
    .a(_8_bit_to_4_7_sec_connector_2_o[24]), .b(_8_bit_to_4_7_sec_connector_2_o[23]),
    .c(_8_bit_to_4_7_sec_connector_2_o[22]), .d(_8_bit_to_4_7_sec_connector_2_o[21]),
    .e(_8_bit_to_4_7_sec_connector_2_o[25]), .f(_8_bit_to_4_7_sec_connector_2_o[26]),
    .g(_8_bit_to_4_7_sec_connector_2_o[27]), .dp(1'b0));
  Seven_Seg seven_seg_12 (
    .a(_8_bit_to_4_7_sec_connector_3_o[24]), .b(_8_bit_to_4_7_sec_connector_3_o[23]),
    .c(_8_bit_to_4_7_sec_connector_3_o[22]), .d(_8_bit_to_4_7_sec_connector_3_o[21]),
    .e(_8_bit_to_4_7_sec_connector_3_o[25]), .f(_8_bit_to_4_7_sec_connector_3_o[26]),
    .g(_8_bit_to_4_7_sec_connector_3_o[27]), .dp(1'b0));

  // Notes on the sheet:
  //   A:
  //   A << B
  //   A >> B
  //   A << 1
  //   _*
  //   A + B
  //   A + 1
  //   A - 1
  //   1337_10
  //   B:
  //   0
  //   5
  //   -5
  //   33
  //   tester application for the alu
endmodule
