// Digital circuit half_adder.dig as structural Verilog
module half_adder (
  input  A,
  input  B,
  output S,
  output C_out
);

  xor xor_1 (S, A, B);
  and and_1 (C_out, A, B);

  // Notes on the sheet:
  //   half adder it adds two
  //   input bits together and gives the carry out.
endmodule
