// Digital circuit shift_1_bit_by_one.dig as structural Verilog
module shift_1_bit_by_one (
  input  L,
  input  U,
  input  O,
  output Out
);

  wire and_1_out, and_2_out;

  and and_1 (and_1_out, O, L);
  and and_2 (and_2_out, ~O, U);  // And
  or or_1 (Out, and_1_out, and_2_out);

  // Notes on the sheet:
  //   Either L, the lower bit, or U the upper bit will be the Output,
  //   depending on if O, the direction of the shift, is left or right.
endmodule
