// Digital circuit shift_8_bit_by_8.dig as structural Verilog
module shift_8_bit_by_8 (
  input  [7:0] A,
  input  [7:0] B,
  input  O,
  output [7:0] Y
);

  wire or_1_out;
  wire [7:0] _1_to_8_1_o, _1_to_8_2_o, _1_to_8_3_o, _1_to_8_4_o, _1_to_8_5_o, _1_to_8_6_o, _1_to_8_7_o,
       _1_to_8_8_o, _3_bit_decoder_and_lower_1__0, and_1_out, and_2_out, and_3_out, and_4_out, and_5_out,
       and_6_out, and_7_out, and_8_out, and_9_out, and_10_out, and_11_out, and_12_out, and_13_out,
       and_14_out, and_15_out, shift_8_bit_by_one_1_y, shift_8_bit_by_one_2_y, shift_8_bit_by_one_3_y,
       shift_8_bit_by_one_4_y, shift_8_bit_by_one_5_y, shift_8_bit_by_one_6_y, shift_8_bit_by_one_7_y;

  or or_1 (or_1_out, B[3], B[4], B[5], B[6], B[7]);
  _1_to_8 _1_to_8_1 (.I(or_1_out), .O(_1_to_8_1_o));
  _3_bit_decoder_and_lower _3_bit_decoder_and_lower_1 (.I(B[2:0]), ._0(_3_bit_decoder_and_lower_1__0));
  assign and_1_out = ~_1_to_8_1_o & A;  // And and_1, 8 bits wide
  _1_to_8 _1_to_8_2 (.I(_3_bit_decoder_and_lower_1__0[1]), .O(_1_to_8_2_o));
  assign and_2_out = and_1_out & ~_1_to_8_2_o;  // And and_2, 8 bits wide
  assign and_3_out = _1_to_8_2_o & and_1_out;  // And and_3, 8 bits wide
  shift_8_bit_by_one shift_8_bit_by_one_1 (.A(and_3_out), .O(O), .Y(shift_8_bit_by_one_1_y));
  _1_to_8 _1_to_8_3 (.I(_3_bit_decoder_and_lower_1__0[2]), .O(_1_to_8_3_o));
  assign and_4_out = shift_8_bit_by_one_1_y & ~_1_to_8_3_o;  // And and_4, 8 bits wide
  assign and_5_out = _1_to_8_3_o & shift_8_bit_by_one_1_y;  // And and_5, 8 bits wide
  shift_8_bit_by_one shift_8_bit_by_one_2 (.A(and_5_out), .O(O), .Y(shift_8_bit_by_one_2_y));
  _1_to_8 _1_to_8_4 (.I(_3_bit_decoder_and_lower_1__0[3]), .O(_1_to_8_4_o));
  assign and_6_out = shift_8_bit_by_one_2_y & ~_1_to_8_4_o;  // And and_6, 8 bits wide
  assign and_7_out = _1_to_8_4_o & shift_8_bit_by_one_2_y;  // And and_7, 8 bits wide
  shift_8_bit_by_one shift_8_bit_by_one_3 (.A(and_7_out), .O(O), .Y(shift_8_bit_by_one_3_y));
  _1_to_8 _1_to_8_5 (.I(_3_bit_decoder_and_lower_1__0[4]), .O(_1_to_8_5_o));
  assign and_8_out = shift_8_bit_by_one_3_y & ~_1_to_8_5_o;  // And and_8, 8 bits wide
  assign and_9_out = _1_to_8_5_o & shift_8_bit_by_one_3_y;  // And and_9, 8 bits wide
  shift_8_bit_by_one shift_8_bit_by_one_4 (.A(and_9_out), .O(O), .Y(shift_8_bit_by_one_4_y));
  _1_to_8 _1_to_8_6 (.I(_3_bit_decoder_and_lower_1__0[5]), .O(_1_to_8_6_o));
  assign and_10_out = shift_8_bit_by_one_4_y & ~_1_to_8_6_o;  // And and_10, 8 bits wide
  assign and_11_out = _1_to_8_6_o & shift_8_bit_by_one_4_y;  // And and_11, 8 bits wide
  shift_8_bit_by_one shift_8_bit_by_one_5 (.A(and_11_out), .O(O), .Y(shift_8_bit_by_one_5_y));
  _1_to_8 _1_to_8_7 (.I(_3_bit_decoder_and_lower_1__0[6]), .O(_1_to_8_7_o));
  assign and_12_out = shift_8_bit_by_one_5_y & ~_1_to_8_7_o;  // And and_12, 8 bits wide
  assign and_13_out = _1_to_8_7_o & shift_8_bit_by_one_5_y;  // And and_13, 8 bits wide
  shift_8_bit_by_one shift_8_bit_by_one_6 (.A(and_13_out), .O(O), .Y(shift_8_bit_by_one_6_y));
  _1_to_8 _1_to_8_8 (.I(_3_bit_decoder_and_lower_1__0[7]), .O(_1_to_8_8_o));
  assign and_14_out = shift_8_bit_by_one_6_y & ~_1_to_8_8_o;  // And and_14, 8 bits wide
  assign and_15_out = _1_to_8_8_o & shift_8_bit_by_one_6_y;  // And and_15, 8 bits wide
  shift_8_bit_by_one shift_8_bit_by_one_7 (.A(and_15_out), .O(O), .Y(shift_8_bit_by_one_7_y));
  assign Y = and_2_out | and_4_out | and_6_out | and_8_out | and_10_out | and_12_out | and_14_out | shift_8_bit_by_one_7_y;  // Or or_2, 8 bits wide

  // Notes on the sheet:
  //   If one of the 5 msbs of B  we would shift more than 8 steps. Therfore we set A to 0 if thats the case.
  //   The f3 lsbs of B will be decoded. Each bit of the decode-output will turn on the number of shifters that is represented by the number..
  //   The Input A will be anded once with the negation and once without negation of each bit of the decoder-output (the lsb doesnt matter, since its 2 to the power of 0, which means the input of the decoder
  //   was 0). the latter one will go through a shifter, and the output will be dependant on Input O (the direction of the shift).
  //   A goes through 8 shifts each, depending on if the decoder-output bit for each shift is 1 or not. If its 1, 8bits of 1s will be anded with A and A will be shifted by 1.  If its 0, 8bits of 1s will be anded with A and
  //   A will go to Y through one of the lanes.
endmodule
