// Digital circuit shift_8_bit_by_one.dig as structural Verilog
module shift_8_bit_by_one (
  input  [7:0] A,
  input  O,
  output [7:0] Y
);

  shift_1_bit_by_one shift_1_bit_by_one_1 (.L(1'b0), .U(A[1]), .O(O), .Out(Y[0]));
  shift_1_bit_by_one shift_1_bit_by_one_2 (.L(A[0]), .U(A[2]), .O(O), .Out(Y[1]));
  shift_1_bit_by_one shift_1_bit_by_one_3 (.L(A[1]), .U(A[3]), .O(O), .Out(Y[2]));
  shift_1_bit_by_one shift_1_bit_by_one_4 (.L(A[2]), .U(A[4]), .O(O), .Out(Y[3]));
  shift_1_bit_by_one shift_1_bit_by_one_5 (.L(A[3]), .U(A[5]), .O(O), .Out(Y[4]));
  shift_1_bit_by_one shift_1_bit_by_one_6 (.L(A[4]), .U(A[6]), .O(O), .Out(Y[5]));
  shift_1_bit_by_one shift_1_bit_by_one_7 (.L(A[5]), .U(A[7]), .O(O), .Out(Y[6]));
  shift_1_bit_by_one shift_1_bit_by_one_8 (.L(A[6]), .U(1'b0), .O(O), .Out(Y[7]));

  // Notes on the sheet:
  //   The Input A gets split into its 8 bits. For each bit, theres a shifter. for the nth bit,
  //   if it isnt the lsb or msb, its connected to the n-1th or n+1th shifter. this will be
  //   dependant on O, which will decide the direction of the shift based on if its 1 or 0.
  //   the lsb and msb will of course only be going to the n+1th and n-1th shifter
  //   respectively, while the other input for that shifter will be a 0.
endmodule
