// Digital circuit to_BCD_block.dig as structural Verilog
module to_BCD_block (
  input  x_1,
  input  x_2,
  input  x_3,
  input  x_4,
  output o_1,
  output o_2,
  output o_3,
  output o_4
);

  LookUpTable #(.Bits(4)) lookuptable_1 (.in0(x_1), .in1(x_2), .in2(x_3), .in3(x_4), .out({o_4, o_3, o_2, o_1}));

  // Notes on the sheet:
  //   This converts 4 bits in such a way, that only the
  //   first 9 decimal values will be given out, higher than
  //   nine will turn all output bits false, since we need to skip
  //   6 bits, cause of the hexadecimals, to have 4 bits later
  //   showcase one digit position that doesnt go higher than 9.
  //   contents of lookuptable_1 (hex, n*v repeats v):
  //   0,1,2,3,4,8,9,a,b,c,c0,b0
endmodule
